// Logisim project toyCPU.circ as structural Verilog: 33 circuits, main circuit CPU
module CPU (
  input  in_1,
  output [7:0] out_2,
  output [7:0] out_3,
  output [7:0] out_4,
  output [7:0] out_5,
  output [7:0] BUS_VALUE,
  output [7:0] TMP,
  output [7:0] TMP_BUS,
  output [7:0] M_REG_VAL,
  output [7:0] IR_VAL,
  output [7:0] ALU_OUTPUT,
  output [7:0] IAR_VAL,
  output [7:0] ACC_VAL
);

  wire and_1_out, clock_1_out, cpu_alu_1_a_larger, cpu_alu_1_carryout, cpu_alu_1_equal, cpu_alu_1_zero,
       cpu_alu_flags_1_al_out, cpu_alu_flags_1_c_out, cpu_alu_flags_1_eq_out, cpu_alu_flags_1_z_out,
       cpu_carry_tmp_1_o, cpu_clk_1_clk, cpu_clk_1_clke, cpu_clk_1_clks, cpu_control_section_1_acc_e,
       cpu_control_section_1_acc_s, cpu_control_section_1_bus_1, cpu_control_section_1_flags_s,
       cpu_control_section_1_ground_e, cpu_control_section_1_iar_e, cpu_control_section_1_iar_s,
       cpu_control_section_1_ir_s, cpu_control_section_1_is_step_5, cpu_control_section_1_m_ram_s,
       cpu_control_section_1_op_0, cpu_control_section_1_op_1, cpu_control_section_1_op_2,
       cpu_control_section_1_r0_e, cpu_control_section_1_r0_s, cpu_control_section_1_r1_e,
       cpu_control_section_1_r1_s, cpu_control_section_1_r2_e, cpu_control_section_1_r2_s,
       cpu_control_section_1_r3_e, cpu_control_section_1_r3_s, cpu_control_section_1_ram_e,
       cpu_control_section_1_ram_s, cpu_control_section_1_tmp_s;

  CPU_TMP cpu_tmp_1 (.S(cpu_control_section_1_tmp_s), .I(BUS_VALUE), .O(TMP));
  CPU_BUS cpu_bus_1 (.I(TMP), .in_2(cpu_control_section_1_bus_1), .O(TMP_BUS));
  CPU_ALU cpu_alu_1 (
    .CarryIn(and_1_out), .A(BUS_VALUE), .B(TMP_BUS), .B2(cpu_control_section_1_op_2),
    .B1(cpu_control_section_1_op_1), .B0(cpu_control_section_1_op_0), .ZERO(cpu_alu_1_zero), .O(ALU_OUTPUT),
    .CarryOut(cpu_alu_1_carryout), .A_Larger(cpu_alu_1_a_larger), .EQUAL(cpu_alu_1_equal));
  CPU_ACCUMULATOR cpu_accumulator_1 (
    .I(ALU_OUTPUT), .S(cpu_control_section_1_acc_s), .E(cpu_control_section_1_acc_e), .REG_VAL(ACC_VAL),
    .O(BUS_VALUE));
  and and_1 (and_1_out, cpu_carry_tmp_1_o, cpu_control_section_1_is_step_5);
  Clock clock_1 (.out(clock_1_out));
  CPU_CARRY_TMP cpu_carry_tmp_1 (.C(cpu_alu_flags_1_c_out), .S(cpu_control_section_1_tmp_s), .O(cpu_carry_tmp_1_o));
  CPU_ALU_FLAGS cpu_alu_flags_1 (
    .C(cpu_alu_1_carryout), .AL(cpu_alu_1_a_larger), .EQ(cpu_alu_1_equal), .Z(cpu_alu_1_zero),
    .S(cpu_control_section_1_flags_s), .C_OUT(cpu_alu_flags_1_c_out), .AL_OUT(cpu_alu_flags_1_al_out),
    .EQ_OUT(cpu_alu_flags_1_eq_out), .Z_OUT(cpu_alu_flags_1_z_out));
  CPU_CONTROL_SECTION cpu_control_section_1 (
    .CLKS(cpu_clk_1_clks), .CLK(cpu_clk_1_clk), .CLKE(cpu_clk_1_clke), .Reset_CPU(in_1), .IR_IN(IR_VAL),
    .C(cpu_alu_flags_1_c_out), .AL(cpu_alu_flags_1_al_out), .EQ(cpu_alu_flags_1_eq_out),
    .Z(cpu_alu_flags_1_z_out), .OP_2(cpu_control_section_1_op_2), .OP_1(cpu_control_section_1_op_1),
    .OP_0(cpu_control_section_1_op_0), .BUS_1(cpu_control_section_1_bus_1),
    .RAM_E(cpu_control_section_1_ram_e), .ACC_E(cpu_control_section_1_acc_e),
    .IAR_E(cpu_control_section_1_iar_e), .R0_E(cpu_control_section_1_r0_e),
    .R1_E(cpu_control_section_1_r1_e), .R2_E(cpu_control_section_1_r2_e), .R3_E(cpu_control_section_1_r3_e),
    .IS_STEP_5(cpu_control_section_1_is_step_5), .GROUND_E(cpu_control_section_1_ground_e),
    .IR_S(cpu_control_section_1_ir_s), .IAR_S(cpu_control_section_1_iar_s),
    .R0_S(cpu_control_section_1_r0_s), .R1_S(cpu_control_section_1_r1_s), .R2_S(cpu_control_section_1_r2_s),
    .R3_S(cpu_control_section_1_r3_s), .M_RAM_S(cpu_control_section_1_m_ram_s),
    .ACC_S(cpu_control_section_1_acc_s), .RAM_S(cpu_control_section_1_ram_s),
    .TMP_S(cpu_control_section_1_tmp_s), .FLAGS_S(cpu_control_section_1_flags_s));
  CPU_CLK cpu_clk_1 (.CLKIN(clock_1_out), .CLK(cpu_clk_1_clk), .CLKS(cpu_clk_1_clks), .CLKE(cpu_clk_1_clke));
  CPU_ENABLER cpu_enabler_1 (.I({8{1'b0}}), .E(cpu_control_section_1_ground_e), .O(BUS_VALUE));
  CPU_REGISTER_8 cpu_register_8_1 (
    .I(BUS_VALUE), .S(cpu_control_section_1_r0_s), .E(cpu_control_section_1_r0_e), .O(BUS_VALUE),
    .REG_VAL(out_2));
  CPU_REGISTER_8 cpu_register_8_2 (
    .I(BUS_VALUE), .S(cpu_control_section_1_r1_s), .E(cpu_control_section_1_r1_e), .O(BUS_VALUE),
    .REG_VAL(out_3));
  CPU_IAR_REG cpu_iar_reg_1 (
    .I(BUS_VALUE), .S(cpu_control_section_1_iar_s), .E(cpu_control_section_1_iar_e), .REG_VAL(IAR_VAL),
    .O(BUS_VALUE));
  CPU_REGISTER_8 cpu_register_8_3 (
    .I(BUS_VALUE), .S(cpu_control_section_1_r2_s), .E(cpu_control_section_1_r2_e), .O(BUS_VALUE),
    .REG_VAL(out_4));
  CPU_IR cpu_ir_1 (.I(BUS_VALUE), .S(cpu_control_section_1_ir_s), .O(IR_VAL));
  CPU_REGISTER_8 cpu_register_8_4 (
    .I(BUS_VALUE), .S(cpu_control_section_1_r3_s), .E(cpu_control_section_1_r3_e), .O(BUS_VALUE),
    .REG_VAL(out_5));
  CPU_RAM_256 cpu_ram_256_1 (
    .S(cpu_control_section_1_ram_s), .E(cpu_control_section_1_ram_e), .address(BUS_VALUE),
    .sa(cpu_control_section_1_m_ram_s), .I(BUS_VALUE), .REG_VAL(M_REG_VAL), .O(BUS_VALUE));
endmodule

module CPU_CONTROL_SECTION (
  input  CLKS,
  input  CLK,
  input  Reset_CPU,
  input  CLKE,
  input  C,
  input  AL,
  input  EQ,
  input  Z,
  input  [7:0] IR_IN,
  output BUS_1,
  output RAM_E,
  output M_RAM_S,
  output ACC_E,
  output ACC_S,
  output IS_STEP_5,
  output IAR_E,
  output RAM_S,
  output TMP_S,
  output R0_E,
  output FLAGS_S,
  output R1_E,
  output R2_E,
  output R3_E,
  output IR_S,
  output IAR_S,
  output R0_S,
  output R1_S,
  output R2_S,
  output R3_S,
  output GROUND_E,
  output OP_2,
  output OP_1,
  output OP_0
);

  wire ACC_E_t, ACC_S_t, and_5_out, and_6_out, and_7_out, and_8_out, and_9_out, and_10_out, and_11_out,
       and_12_out, and_13_out, and_17_out, and_26_out, and_27_out, and_28_out, and_29_out, and_49_out,
       and_50_out, and_51_out, and_52_out, and_53_out, and_54_out, and_55_out, and_56_out, and_57_out,
       and_58_out, and_59_out, BUS_1_E, cpu_stepper_1_s7, decoder_2_out0, decoder_2_out1, decoder_2_out2,
       decoder_2_out3, decoder_3_out0, decoder_3_out1, decoder_3_out2, decoder_3_out3, decoder_3_out4,
       decoder_3_out5, decoder_3_out6, decoder_3_out7, FLAGS_S_t, IAR_E_t, IAR_S_t, IR_S_t, IS_CLEAR_FLAGS,
       IS_DATA, IS_JUMP_ADDR, IS_JUMP_IF, IS_JUMP_IF_CONDITION, IS_JUMP_REG, IS_LOAD, IS_STORE, M_RAM_S_t,
       not_1_out, not_2_out, not_3_out, not_4_out, NOT_CMP, or_1_out, or_7_out, or_15_out, RAM_E_t, RAM_S_t,
       REG_A_E, REG_B_0, REG_B_1, REG_B_2, REG_B_3, REG_B_E, REG_B_S, STEP_1, STEP_3, STEP_4, STEP_4_ALU,
       STEP_4_CLEAR_FLAGS, STEP_4_DATA, STEP_4_JUMP_ADDR, STEP_4_JUMP_IF, STEP_4_JUMP_REG, STEP_4_LOAD,
       STEP_4_STORE, STEP_5_ALU, STEP_5_DATA, STEP_5_JUMP_ADDR, STEP_5_JUMP_IF, STEP_5_LOAD, STEP_6,
       STEP_6_ALU, STEP_6_DATA, STEP_6_JUMP_IF, STEP_6_LOAD, STEP_6_STORE;

  or or_1 (or_1_out, R3_E, R2_E, R1_E, R0_E, IAR_E, ACC_E, RAM_E);
  not not_1 (not_1_out, or_1_out);
  and and_1 (BUS_1, not_2_out, BUS_1_E);
  or or_2 (R0_E, and_5_out, and_9_out);
  or or_3 (R1_E, and_6_out, and_10_out);
  or or_4 (R2_E, and_7_out, and_11_out);
  or or_5 (R3_E, and_8_out, and_12_out);
  not not_2 (not_2_out, Reset_CPU);
  or or_6 (GROUND_E, or_7_out, Reset_CPU);
  and and_2 (RAM_E, and_13_out, RAM_E_t);
  and and_3 (ACC_E, and_13_out, ACC_E_t);
  and and_4 (IAR_E, and_13_out, IAR_E_t);
  and and_5 (and_5_out, and_13_out, REG_B_0, REG_B_E);
  and and_6 (and_6_out, and_13_out, REG_B_1, REG_B_E);
  and and_7 (and_7_out, and_13_out, REG_B_2, REG_B_E);
  and and_8 (and_8_out, and_13_out, REG_B_3, REG_B_E);
  and and_9 (and_9_out, and_13_out, decoder_2_out0, REG_A_E);
  and and_10 (and_10_out, and_13_out, decoder_2_out1, REG_A_E);
  and and_11 (and_11_out, and_13_out, decoder_2_out2, REG_A_E);
  and and_12 (and_12_out, and_13_out, decoder_2_out3, REG_A_E);
  or or_7 (or_7_out, not_1_out, not_3_out);
  and and_13 (and_13_out, not_2_out, CLKE);
  not not_3 (not_3_out, and_13_out);
  and and_14 (OP_2, IR_IN[6], IS_STEP_5, IR_IN[7]);
  and and_15 (OP_1, IR_IN[5], IS_STEP_5, IR_IN[7]);
  and and_16 (OP_0, IR_IN[4], IS_STEP_5, IR_IN[7]);
  Decoder #(.enable("false"), .select(2)) decoder_1 (
    .out0(REG_B_0), .out1(REG_B_1), .out2(REG_B_2), .out3(REG_B_3), .sel(IR_IN[1:0]));
  Decoder #(.enable("false"), .select(2)) decoder_2 (
    .out0(decoder_2_out0), .out1(decoder_2_out1), .out2(decoder_2_out2), .out3(decoder_2_out3),
    .sel(IR_IN[3:2]));
  Decoder #(.enable("false"), .select(3)) decoder_3 (
    .out0(decoder_3_out0), .out1(decoder_3_out1), .out2(decoder_3_out2), .out3(decoder_3_out3),
    .out4(decoder_3_out4), .out5(decoder_3_out5), .out6(decoder_3_out6), .out7(decoder_3_out7),
    .sel(IR_IN[6:4]));
  not not_4 (not_4_out, IR_IN[7]);
  and and_17 (and_17_out, IR_IN[6], IR_IN[5], IR_IN[4]);
  and and_18 (IS_LOAD, not_4_out, decoder_3_out0);
  and and_19 (IS_STORE, not_4_out, decoder_3_out1);
  and and_20 (IS_DATA, not_4_out, decoder_3_out2);
  and and_21 (IS_JUMP_REG, not_4_out, decoder_3_out3);
  and and_22 (IS_JUMP_ADDR, not_4_out, decoder_3_out4);
  and and_23 (IS_JUMP_IF, not_4_out, decoder_3_out5);
  and and_24 (IS_CLEAR_FLAGS, not_4_out, decoder_3_out6);
  // AND_Gate and_25 has open pins: in0=not_4_out, in1=decoder_3_out7, out=open
  not not_5 (NOT_CMP, and_17_out);
  and and_26 (and_26_out, C, IR_IN[3]);
  and and_27 (and_27_out, AL, IR_IN[2]);
  and and_28 (and_28_out, EQ, IR_IN[1]);
  and and_29 (and_29_out, Z, IR_IN[0]);
  or or_8 (IS_JUMP_IF_CONDITION, and_26_out, and_27_out, and_28_out, and_29_out);
  or or_9 (BUS_1_E, STEP_1, STEP_4_JUMP_IF, STEP_4_CLEAR_FLAGS, STEP_4_DATA);
  or or_10 (RAM_E_t, STEP_5_LOAD, STEP_6_JUMP_IF, IR_S_t, STEP_5_JUMP_ADDR, STEP_5_DATA);
  or or_11 (ACC_E_t, STEP_3, STEP_5_JUMP_IF, STEP_6_ALU, STEP_6_DATA);
  or or_12 (IAR_E_t, STEP_1, STEP_4_DATA, STEP_4_JUMP_ADDR, STEP_4_JUMP_IF);
  or or_13 (REG_A_E, STEP_4_LOAD, STEP_4_STORE, STEP_5_ALU);
  or or_14 (REG_B_E, STEP_4_ALU, STEP_4_JUMP_REG, RAM_S_t);
  CPU_STEPPER cpu_stepper_1 (
    .reset(or_15_out), .clk(CLK), .S4(STEP_4), .S5(IS_STEP_5), .S6(STEP_6), .S7(cpu_stepper_1_s7),
    .S1(STEP_1), .S2(IR_S_t), .S3(STEP_3));
  or or_15 (or_15_out, Reset_CPU, cpu_stepper_1_s7);
  and and_30 (STEP_4_ALU, IR_IN[7], STEP_4);
  and and_31 (STEP_4_LOAD, IS_LOAD, STEP_4);
  and and_32 (STEP_4_STORE, IS_STORE, STEP_4);
  and and_33 (STEP_4_DATA, IS_DATA, STEP_4);
  and and_34 (STEP_4_JUMP_REG, IS_JUMP_REG, STEP_4);
  and and_35 (STEP_4_JUMP_ADDR, IS_JUMP_ADDR, STEP_4);
  and and_36 (STEP_4_JUMP_IF, IS_JUMP_IF, STEP_4);
  and and_37 (STEP_4_CLEAR_FLAGS, IS_CLEAR_FLAGS, STEP_4);
  and and_38 (STEP_5_ALU, IR_IN[7], IS_STEP_5);
  and and_39 (STEP_5_LOAD, IS_LOAD, IS_STEP_5);
  and and_40 (RAM_S_t, IS_STORE, IS_STEP_5);
  and and_41 (STEP_5_DATA, IS_DATA, IS_STEP_5);
  and and_42 (STEP_5_JUMP_ADDR, IS_JUMP_ADDR, IS_STEP_5);
  and and_43 (STEP_5_JUMP_IF, IS_JUMP_IF, IS_STEP_5);
  and and_44 (STEP_6_ALU, IR_IN[7], STEP_6);
  and and_45 (STEP_6_LOAD, IS_LOAD, STEP_6);
  and and_46 (STEP_6_STORE, IS_STORE, STEP_6);
  and and_47 (STEP_6_DATA, IS_DATA, STEP_6);
  and and_48 (STEP_6_JUMP_IF, IS_JUMP_IF, IS_JUMP_IF_CONDITION, STEP_6);
  or or_16 (M_RAM_S_t, STEP_1, STEP_4_LOAD, STEP_4_STORE, STEP_4_JUMP_ADDR, STEP_4_DATA, STEP_4_JUMP_IF);
  or or_17 (ACC_S_t, STEP_1, STEP_4_DATA, STEP_4_JUMP_IF, STEP_5_ALU);
  or or_18 (IAR_S_t, STEP_3, STEP_4_JUMP_REG, STEP_5_JUMP_ADDR, STEP_6_JUMP_IF, STEP_5_JUMP_IF, STEP_6_DATA);
  or or_19 (REG_B_S, STEP_5_LOAD, STEP_5_DATA, STEP_6_ALU);
  or or_20 (FLAGS_S_t, STEP_4_CLEAR_FLAGS, STEP_5_ALU);
  and and_49 (and_49_out, CLKS, M_RAM_S_t);
  and and_50 (and_50_out, CLKS, ACC_S_t);
  and and_51 (and_51_out, CLKS, RAM_S_t);
  and and_52 (and_52_out, CLKS, STEP_4_ALU);
  and and_53 (and_53_out, CLKS, FLAGS_S_t);
  and and_54 (and_54_out, CLKS, IR_S_t);
  and and_55 (and_55_out, CLKS, IAR_S_t);
  and and_56 (and_56_out, CLKS, REG_B_0, REG_B_S);
  and and_57 (and_57_out, CLKS, REG_B_1, REG_B_S);
  and and_58 (and_58_out, CLKS, REG_B_2, REG_B_S);
  and and_59 (and_59_out, CLKS, REG_B_3, REG_B_S);
  or or_21 (M_RAM_S, Reset_CPU, and_49_out);
  or or_22 (ACC_S, Reset_CPU, and_50_out);
  or or_23 (RAM_S, Reset_CPU, and_51_out);
  or or_24 (TMP_S, Reset_CPU, and_52_out);
  or or_25 (FLAGS_S, Reset_CPU, and_53_out);
  or or_26 (IR_S, Reset_CPU, and_54_out);
  or or_27 (IAR_S, Reset_CPU, and_55_out);
  or or_28 (R0_S, Reset_CPU, and_56_out);
  or or_29 (R1_S, Reset_CPU, and_57_out);
  or or_30 (R2_S, Reset_CPU, and_58_out);
  or or_31 (R3_S, Reset_CPU, and_59_out);

  // Other names for the same wires on the sheet: IS_ALU = IR_IN[7]; RESET = Reset_CPU; STEP_2 = IR_S_t;
  //   STEP_5 = IS_STEP_5; STEP_5_STORE = RAM_S_t; TMP_S_t = STEP_4_ALU

  // Notes on the sheet:
  //   INSTRUCTION DECODING
  //   REG_B
  //   REG A
  //   ENABLERS
  //   INSTRUCTION PROCESSING
  //   SETTERS
endmodule

module CPU_STEPPER (
  input  reset,
  input  clk,
  output S2,
  output S3,
  output S4,
  output S5,
  output S6,
  output S1,
  output S7
);

  wire d_ff_1_q, d_ff_2_q, d_ff_3_q, d_ff_4_q, d_ff_5_q, d_ff_6_q, d_ff_7_q, d_ff_8_q, d_ff_9_q, d_ff_10_q,
       d_ff_11_q, not_1_out, not_2_out, not_3_out, not_4_out, not_5_out, not_6_out, not_7_out, not_8_out,
       or_1_out, or_2_out;

  not not_1 (not_1_out, clk);
  not not_2 (not_2_out, reset);
  or or_1 (or_1_out, reset, clk);
  or or_2 (or_2_out, reset, not_1_out);
  D_Flip_Flop #(.trigger("high")) d_ff_1 (.D(not_2_out), .clk(or_1_out), .Q(d_ff_1_q));  // open: Qn, preset, reset
  or or_3 (S1, reset, not_3_out);
  D_Flip_Flop #(.trigger("high")) d_ff_2 (.D(d_ff_1_q), .clk(or_2_out), .Q(d_ff_2_q));  // open: Qn, preset, reset
  not not_3 (not_3_out, d_ff_2_q);
  D_Flip_Flop #(.trigger("high")) d_ff_3 (.D(d_ff_2_q), .clk(or_1_out), .Q(d_ff_3_q));  // open: Qn, preset, reset
  and and_1 (S2, d_ff_2_q, not_4_out);
  not not_4 (not_4_out, d_ff_4_q);
  D_Flip_Flop #(.trigger("high")) d_ff_4 (.D(d_ff_3_q), .clk(or_2_out), .Q(d_ff_4_q));  // open: Qn, preset, reset
  and and_2 (S3, d_ff_4_q, not_5_out);
  D_Flip_Flop #(.trigger("high")) d_ff_5 (.D(d_ff_4_q), .clk(or_1_out), .Q(d_ff_5_q));  // open: Qn, preset, reset
  not not_5 (not_5_out, d_ff_6_q);
  D_Flip_Flop #(.trigger("high")) d_ff_6 (.D(d_ff_5_q), .clk(or_2_out), .Q(d_ff_6_q));  // open: Qn, preset, reset
  D_Flip_Flop #(.trigger("high")) d_ff_7 (.D(d_ff_6_q), .clk(or_1_out), .Q(d_ff_7_q));  // open: Qn, preset, reset
  and and_3 (S4, d_ff_6_q, not_6_out);
  D_Flip_Flop #(.trigger("high")) d_ff_8 (.D(d_ff_7_q), .clk(or_2_out), .Q(d_ff_8_q));  // open: Qn, preset, reset
  not not_6 (not_6_out, d_ff_8_q);
  D_Flip_Flop #(.trigger("high")) d_ff_9 (.D(d_ff_8_q), .clk(or_1_out), .Q(d_ff_9_q));  // open: Qn, preset, reset
  and and_4 (S5, d_ff_8_q, not_7_out);
  D_Flip_Flop #(.trigger("high")) d_ff_10 (.D(d_ff_9_q), .clk(or_2_out), .Q(d_ff_10_q));  // open: Qn, preset, reset
  not not_7 (not_7_out, d_ff_10_q);
  D_Flip_Flop #(.trigger("high")) d_ff_11 (.D(d_ff_10_q), .clk(or_1_out), .Q(d_ff_11_q));  // open: Qn, preset, reset
  and and_5 (S6, d_ff_10_q, not_8_out);
  not not_8 (not_8_out, S7);
  D_Flip_Flop #(.trigger("high")) d_ff_12 (.D(d_ff_11_q), .clk(or_2_out), .Q(S7));  // open: Qn, preset, reset
endmodule

module CPU_MEM_1_BIT (
  input  I,
  input  S,
  output Q
);

  wire nand_1_out, nand_2_out, nand_4_out;

  nand nand_1 (nand_1_out, I, S);
  nand nand_2 (nand_2_out, nand_1_out, S);
  nand nand_3 (Q, nand_1_out, nand_4_out);
  nand nand_4 (nand_4_out, Q, nand_2_out);
endmodule

module CPU_MEM_8_BIT (
  input  [7:0] I,
  input  S,
  output [7:0] O
);

  CPU_MEM_1_BIT cpu_mem_1_bit_1 (.I(I[0]), .S(S), .Q(O[0]));
  CPU_MEM_1_BIT cpu_mem_1_bit_2 (.I(I[1]), .S(S), .Q(O[1]));
  CPU_MEM_1_BIT cpu_mem_1_bit_3 (.I(I[2]), .S(S), .Q(O[2]));
  CPU_MEM_1_BIT cpu_mem_1_bit_4 (.I(I[3]), .S(S), .Q(O[3]));
  CPU_MEM_1_BIT cpu_mem_1_bit_5 (.I(I[4]), .S(S), .Q(O[4]));
  CPU_MEM_1_BIT cpu_mem_1_bit_6 (.I(I[5]), .S(S), .Q(O[5]));
  CPU_MEM_1_BIT cpu_mem_1_bit_7 (.I(I[6]), .S(S), .Q(O[6]));
  CPU_MEM_1_BIT cpu_mem_1_bit_8 (.I(I[7]), .S(S), .Q(O[7]));
endmodule

module CPU_TMP (
  input  [7:0] I,
  input  S,
  output [7:0] O
);

  wire [7:0] controlled_buffer_1_out;

  assign controlled_buffer_1_out = S ? I : 8'bz;  // Controlled_Buffer controlled_buffer_1
  CPU_MEM_8_BIT cpu_mem_8_bit_1 (.I(controlled_buffer_1_out), .S(S), .O(O));
endmodule

module CPU_BUS (
  input  [7:0] I,
  input  in_2,
  output [7:0] O
);

  wire not_1_out;

  and and_1 (O[7], I[7], not_1_out);
  and and_2 (O[6], I[6], not_1_out);
  and and_3 (O[5], I[5], not_1_out);
  and and_4 (O[4], I[4], not_1_out);
  and and_5 (O[3], I[3], not_1_out);
  and and_6 (O[2], I[2], not_1_out);
  and and_7 (O[1], I[1], not_1_out);
  or or_1 (O[0], I[0], in_2);
  not not_1 (not_1_out, in_2);
endmodule

module CPU_ENABLER (
  input  [7:0] I,
  input  E,
  output [7:0] O
);

  wire and_1_out, and_2_out, and_3_out, and_4_out, and_5_out, and_6_out, and_7_out, and_8_out;

  and and_1 (and_1_out, I[0], E);
  assign O[0] = E ? and_1_out : 1'bz;  // Controlled_Buffer controlled_buffer_1
  and and_2 (and_2_out, I[1], E);
  assign O[1] = E ? and_2_out : 1'bz;  // Controlled_Buffer controlled_buffer_2
  and and_3 (and_3_out, I[2], E);
  assign O[2] = E ? and_3_out : 1'bz;  // Controlled_Buffer controlled_buffer_3
  and and_4 (and_4_out, I[3], E);
  assign O[3] = E ? and_4_out : 1'bz;  // Controlled_Buffer controlled_buffer_4
  and and_5 (and_5_out, I[4], E);
  assign O[4] = E ? and_5_out : 1'bz;  // Controlled_Buffer controlled_buffer_5
  and and_6 (and_6_out, I[5], E);
  assign O[5] = E ? and_6_out : 1'bz;  // Controlled_Buffer controlled_buffer_6
  and and_7 (and_7_out, I[6], E);
  assign O[6] = E ? and_7_out : 1'bz;  // Controlled_Buffer controlled_buffer_7
  and and_8 (and_8_out, I[7], E);
  assign O[7] = E ? and_8_out : 1'bz;  // Controlled_Buffer controlled_buffer_8
endmodule

module CPU_REGISTER_8 (
  input  [7:0] I,
  input  S,
  input  E,
  output [7:0] REG_VAL,
  output [7:0] O
);

  wire [7:0] cpu_enabler_1_o;

  Register #(.trigger("high")) register_1 (.D(I), .clk(S), .Q(REG_VAL));  // open: en, clr
  CPU_ENABLER cpu_enabler_1 (.I(REG_VAL), .E(E), .O(cpu_enabler_1_o));
  assign O = E ? cpu_enabler_1_o : 8'bz;  // Controlled_Buffer controlled_buffer_1
endmodule

module CPU_REGISTER_8_CUSTOM (
  input  [7:0] I,
  input  S,
  input  E,
  output [7:0] out_4,
  output [7:0] REG_VAL,
  output [7:0] O
);

  wire [7:0] cpu_enabler_1_o;

  CPU_MEM_8_BIT cpu_mem_8_bit_1 (.I(I), .S(S), .O(REG_VAL));
  CPU_ENABLER cpu_enabler_1 (.I(REG_VAL), .E(E), .O(cpu_enabler_1_o));
  assign O = E ? cpu_enabler_1_o : 8'bz;  // Controlled_Buffer controlled_buffer_1

  assign out_4 = I;

  // Notes on the sheet:
  //   8 bit CPU register. Not used on the actual CPU all over the place because LogiSims simulation cannot handle NAND gates which fead into one another
endmodule

module CPU_IAR_REG (
  input  [7:0] I,
  input  S,
  input  E,
  output [7:0] REG_VAL,
  output [7:0] O
);

  CPU_REGISTER_8 cpu_register_8_1 (.I(I), .S(S), .E(E), .O(O), .REG_VAL(REG_VAL));
endmodule

module CPU_IR (
  input  [7:0] I,
  input  S,
  output [7:0] O
);

  CPU_MEM_8_BIT cpu_mem_8_bit_1 (.I(I), .S(S), .O(O));
endmodule

module CPU_ACCUMULATOR (
  input  [7:0] I,
  input  S,
  input  E,
  output [7:0] REG_VAL,
  output [7:0] O
);

  CPU_REGISTER_8_CUSTOM cpu_register_8_custom_1 (.I(I), .S(S), .E(E), .O(O), .REG_VAL(REG_VAL));  // open: out_4
endmodule

module CPU_REG_BYTE (
  input  [7:0] I,
  input  RESET,
  input  H,
  input  V,
  input  S,
  input  E,
  output [7:0] OP,
  output [7:0] O
);

  wire and_1_out, and_2_out, and_3_out, or_1_out;
  wire [7:0] cpu_register_8_custom_1_o;

  and and_1 (and_1_out, H, V);
  and and_2 (and_2_out, and_1_out, S);
  and and_3 (and_3_out, and_1_out, E);
  or or_1 (or_1_out, RESET, and_2_out);
  CPU_REGISTER_8_CUSTOM cpu_register_8_custom_1 (
    .I(I), .S(or_1_out), .E(and_3_out), .O(cpu_register_8_custom_1_o), .REG_VAL(OP));  // open: out_4
  assign O = and_3_out ? cpu_register_8_custom_1_o : 8'bz;  // Controlled_Buffer controlled_buffer_1
endmodule

module CPU_RAM_256 (
  input  [7:0] address,
  input  sa,
  input  S,
  input  E,
  input  [7:0] I,
  output [7:0] REG_VAL,
  output [7:0] O
);

  wire [7:0] cpu_register_8_1_o, ram_1_dout;

  CPU_REGISTER_8 cpu_register_8_1 (.I(address), .S(sa), .E(1'b1), .O(cpu_register_8_1_o), .REG_VAL(REG_VAL));
  RAM #(.trigger("high")) ram_1 (.addr(cpu_register_8_1_o), .we(S), .oe(E), .din(I), .dout(ram_1_dout));
  CPU_ENABLER cpu_enabler_1 (.I(ram_1_dout), .E(E), .O(O));
endmodule

module CPU_RAM_256_CUSTOM (
  input  [7:0] address,
  input  sa,
  input  [7:0] I,
  input  RESET,
  input  S,
  input  E,
  output [7:0] O
);

  wire cpu_decoder_4x16_1_out_2, cpu_decoder_4x16_1_out_3, cpu_decoder_4x16_1_out_4,
       cpu_decoder_4x16_1_out_5, cpu_decoder_4x16_1_out_6, cpu_decoder_4x16_1_out_7,
       cpu_decoder_4x16_1_out_8, cpu_decoder_4x16_1_out_9, cpu_decoder_4x16_1_out_10,
       cpu_decoder_4x16_1_out_11, cpu_decoder_4x16_1_out_12, cpu_decoder_4x16_1_out_13,
       cpu_decoder_4x16_1_out_14, cpu_decoder_4x16_1_out_15, cpu_decoder_4x16_1_out_16,
       cpu_decoder_4x16_1_out_17, cpu_decoder_4x16_2_out_2, cpu_decoder_4x16_2_out_3,
       cpu_decoder_4x16_2_out_4, cpu_decoder_4x16_2_out_5, cpu_decoder_4x16_2_out_6,
       cpu_decoder_4x16_2_out_7, cpu_decoder_4x16_2_out_8, cpu_decoder_4x16_2_out_9,
       cpu_decoder_4x16_2_out_10, cpu_decoder_4x16_2_out_11, cpu_decoder_4x16_2_out_12,
       cpu_decoder_4x16_2_out_13, cpu_decoder_4x16_2_out_14, cpu_decoder_4x16_2_out_15,
       cpu_decoder_4x16_2_out_16, cpu_decoder_4x16_2_out_17;
  wire [7:0] cpu_mem_8_bit_1_o, undriven;

  CPU_MEM_8_BIT cpu_mem_8_bit_1 (.I(undriven), .S(sa), .O(cpu_mem_8_bit_1_o));
  CPU_DECODER_4x16 cpu_decoder_4x16_1 (
    .I(cpu_mem_8_bit_1_o[7:4]), .out_13(cpu_decoder_4x16_1_out_13), .out_14(cpu_decoder_4x16_1_out_14),
    .out_15(cpu_decoder_4x16_1_out_15), .out_16(cpu_decoder_4x16_1_out_16),
    .out_17(cpu_decoder_4x16_1_out_17), .out_2(cpu_decoder_4x16_1_out_2), .out_3(cpu_decoder_4x16_1_out_3),
    .out_4(cpu_decoder_4x16_1_out_4), .out_5(cpu_decoder_4x16_1_out_5), .out_6(cpu_decoder_4x16_1_out_6),
    .out_7(cpu_decoder_4x16_1_out_7), .out_8(cpu_decoder_4x16_1_out_8), .out_9(cpu_decoder_4x16_1_out_9),
    .out_10(cpu_decoder_4x16_1_out_10), .out_11(cpu_decoder_4x16_1_out_11), .out_12(cpu_decoder_4x16_1_out_12));
  CPU_REG_BYTE cpu_reg_byte_1 (
    .H(cpu_decoder_4x16_1_out_2), .V(cpu_decoder_4x16_2_out_17), .S(S), .E(E), .I(I), .RESET(RESET), .O(O));  // open: OP
  CPU_REG_BYTE cpu_reg_byte_2 (
    .H(cpu_decoder_4x16_1_out_3), .V(cpu_decoder_4x16_2_out_17), .S(S), .E(E), .I(I), .RESET(RESET), .O(O));  // open: OP
  CPU_REG_BYTE cpu_reg_byte_3 (
    .H(cpu_decoder_4x16_1_out_4), .V(cpu_decoder_4x16_2_out_17), .S(S), .E(E), .I(I), .RESET(RESET), .O(O));  // open: OP
  CPU_REG_BYTE cpu_reg_byte_4 (
    .H(cpu_decoder_4x16_1_out_5), .V(cpu_decoder_4x16_2_out_17), .S(S), .E(E), .I(I), .RESET(RESET), .O(O));  // open: OP
  CPU_REG_BYTE cpu_reg_byte_5 (
    .H(cpu_decoder_4x16_1_out_6), .V(cpu_decoder_4x16_2_out_17), .S(S), .E(E), .I(I), .RESET(RESET), .O(O));  // open: OP
  CPU_REG_BYTE cpu_reg_byte_6 (
    .H(cpu_decoder_4x16_1_out_7), .V(cpu_decoder_4x16_2_out_17), .S(S), .E(E), .I(I), .RESET(RESET), .O(O));  // open: OP
  CPU_REG_BYTE cpu_reg_byte_7 (
    .H(cpu_decoder_4x16_1_out_8), .V(cpu_decoder_4x16_2_out_17), .S(S), .E(E), .I(I), .RESET(RESET), .O(O));  // open: OP
  CPU_REG_BYTE cpu_reg_byte_8 (
    .H(cpu_decoder_4x16_1_out_9), .V(cpu_decoder_4x16_2_out_17), .S(S), .E(E), .I(I), .RESET(RESET), .O(O));  // open: OP
  CPU_REG_BYTE cpu_reg_byte_9 (
    .H(cpu_decoder_4x16_1_out_10), .V(cpu_decoder_4x16_2_out_17), .S(S), .E(E), .I(I), .RESET(RESET), .O(O));  // open: OP
  CPU_REG_BYTE cpu_reg_byte_10 (
    .H(cpu_decoder_4x16_1_out_11), .V(cpu_decoder_4x16_2_out_17), .S(S), .E(E), .I(I), .RESET(RESET), .O(O));  // open: OP
  CPU_REG_BYTE cpu_reg_byte_11 (
    .H(cpu_decoder_4x16_1_out_12), .V(cpu_decoder_4x16_2_out_17), .S(S), .E(E), .I(I), .RESET(RESET), .O(O));  // open: OP
  CPU_REG_BYTE cpu_reg_byte_12 (
    .H(cpu_decoder_4x16_1_out_13), .V(cpu_decoder_4x16_2_out_17), .S(S), .E(E), .I(I), .RESET(RESET), .O(O));  // open: OP
  CPU_REG_BYTE cpu_reg_byte_13 (
    .H(cpu_decoder_4x16_1_out_14), .V(cpu_decoder_4x16_2_out_17), .S(S), .E(E), .I(I), .RESET(RESET), .O(O));  // open: OP
  CPU_REG_BYTE cpu_reg_byte_14 (
    .H(cpu_decoder_4x16_1_out_15), .V(cpu_decoder_4x16_2_out_17), .S(S), .E(E), .I(I), .RESET(RESET), .O(O));  // open: OP
  CPU_REG_BYTE cpu_reg_byte_15 (
    .H(cpu_decoder_4x16_1_out_16), .V(cpu_decoder_4x16_2_out_17), .S(S), .E(E), .I(I), .RESET(RESET), .O(O));  // open: OP
  CPU_REG_BYTE cpu_reg_byte_16 (
    .H(cpu_decoder_4x16_1_out_17), .V(cpu_decoder_4x16_2_out_17), .S(S), .E(E), .I(I), .RESET(RESET), .O(O));  // open: OP
  CPU_REG_BYTE cpu_reg_byte_17 (
    .H(cpu_decoder_4x16_1_out_2), .V(cpu_decoder_4x16_2_out_16), .S(S), .E(E), .I(I), .RESET(RESET), .O(O));  // open: OP
  CPU_REG_BYTE cpu_reg_byte_18 (
    .H(cpu_decoder_4x16_1_out_3), .V(cpu_decoder_4x16_2_out_16), .S(S), .E(E), .I(I), .RESET(RESET), .O(O));  // open: OP
  CPU_REG_BYTE cpu_reg_byte_19 (
    .H(cpu_decoder_4x16_1_out_4), .V(cpu_decoder_4x16_2_out_16), .S(S), .E(E), .I(I), .RESET(RESET), .O(O));  // open: OP
  CPU_REG_BYTE cpu_reg_byte_20 (
    .H(cpu_decoder_4x16_1_out_5), .V(cpu_decoder_4x16_2_out_16), .S(S), .E(E), .I(I), .RESET(RESET), .O(O));  // open: OP
  CPU_REG_BYTE cpu_reg_byte_21 (
    .H(cpu_decoder_4x16_1_out_6), .V(cpu_decoder_4x16_2_out_16), .S(S), .E(E), .I(I), .RESET(RESET), .O(O));  // open: OP
  CPU_REG_BYTE cpu_reg_byte_22 (
    .H(cpu_decoder_4x16_1_out_7), .V(cpu_decoder_4x16_2_out_16), .S(S), .E(E), .I(I), .RESET(RESET), .O(O));  // open: OP
  CPU_REG_BYTE cpu_reg_byte_23 (
    .H(cpu_decoder_4x16_1_out_8), .V(cpu_decoder_4x16_2_out_16), .S(S), .E(E), .I(I), .RESET(RESET), .O(O));  // open: OP
  CPU_REG_BYTE cpu_reg_byte_24 (
    .H(cpu_decoder_4x16_1_out_9), .V(cpu_decoder_4x16_2_out_16), .S(S), .E(E), .I(I), .RESET(RESET), .O(O));  // open: OP
  CPU_REG_BYTE cpu_reg_byte_25 (
    .H(cpu_decoder_4x16_1_out_10), .V(cpu_decoder_4x16_2_out_16), .S(S), .E(E), .I(I), .RESET(RESET), .O(O));  // open: OP
  CPU_REG_BYTE cpu_reg_byte_26 (
    .H(cpu_decoder_4x16_1_out_11), .V(cpu_decoder_4x16_2_out_16), .S(S), .E(E), .I(I), .RESET(RESET), .O(O));  // open: OP
  CPU_REG_BYTE cpu_reg_byte_27 (
    .H(cpu_decoder_4x16_1_out_12), .V(cpu_decoder_4x16_2_out_16), .S(S), .E(E), .I(I), .RESET(RESET), .O(O));  // open: OP
  CPU_REG_BYTE cpu_reg_byte_28 (
    .H(cpu_decoder_4x16_1_out_13), .V(cpu_decoder_4x16_2_out_16), .S(S), .E(E), .I(I), .RESET(RESET), .O(O));  // open: OP
  CPU_REG_BYTE cpu_reg_byte_29 (
    .H(cpu_decoder_4x16_1_out_14), .V(cpu_decoder_4x16_2_out_16), .S(S), .E(E), .I(I), .RESET(RESET), .O(O));  // open: OP
  CPU_REG_BYTE cpu_reg_byte_30 (
    .H(cpu_decoder_4x16_1_out_15), .V(cpu_decoder_4x16_2_out_16), .S(S), .E(E), .I(I), .RESET(RESET), .O(O));  // open: OP
  CPU_REG_BYTE cpu_reg_byte_31 (
    .H(cpu_decoder_4x16_1_out_16), .V(cpu_decoder_4x16_2_out_16), .S(S), .E(E), .I(I), .RESET(RESET), .O(O));  // open: OP
  CPU_REG_BYTE cpu_reg_byte_32 (
    .H(cpu_decoder_4x16_1_out_17), .V(cpu_decoder_4x16_2_out_16), .S(S), .E(E), .I(I), .RESET(RESET), .O(O));  // open: OP
  CPU_REG_BYTE cpu_reg_byte_33 (
    .H(cpu_decoder_4x16_1_out_2), .V(cpu_decoder_4x16_2_out_15), .S(S), .E(E), .I(I), .RESET(RESET), .O(O));  // open: OP
  CPU_REG_BYTE cpu_reg_byte_34 (
    .H(cpu_decoder_4x16_1_out_3), .V(cpu_decoder_4x16_2_out_15), .S(S), .E(E), .I(I), .RESET(RESET), .O(O));  // open: OP
  CPU_REG_BYTE cpu_reg_byte_35 (
    .H(cpu_decoder_4x16_1_out_4), .V(cpu_decoder_4x16_2_out_15), .S(S), .E(E), .I(I), .RESET(RESET), .O(O));  // open: OP
  CPU_REG_BYTE cpu_reg_byte_36 (
    .H(cpu_decoder_4x16_1_out_5), .V(cpu_decoder_4x16_2_out_15), .S(S), .E(E), .I(I), .RESET(RESET), .O(O));  // open: OP
  CPU_REG_BYTE cpu_reg_byte_37 (
    .H(cpu_decoder_4x16_1_out_6), .V(cpu_decoder_4x16_2_out_15), .S(S), .E(E), .I(I), .RESET(RESET), .O(O));  // open: OP
  CPU_REG_BYTE cpu_reg_byte_38 (
    .H(cpu_decoder_4x16_1_out_7), .V(cpu_decoder_4x16_2_out_15), .S(S), .E(E), .I(I), .RESET(RESET), .O(O));  // open: OP
  CPU_REG_BYTE cpu_reg_byte_39 (
    .H(cpu_decoder_4x16_1_out_8), .V(cpu_decoder_4x16_2_out_15), .S(S), .E(E), .I(I), .RESET(RESET), .O(O));  // open: OP
  CPU_REG_BYTE cpu_reg_byte_40 (
    .H(cpu_decoder_4x16_1_out_9), .V(cpu_decoder_4x16_2_out_15), .S(S), .E(E), .I(I), .RESET(RESET), .O(O));  // open: OP
  CPU_REG_BYTE cpu_reg_byte_41 (
    .H(cpu_decoder_4x16_1_out_10), .V(cpu_decoder_4x16_2_out_15), .S(S), .E(E), .I(I), .RESET(RESET), .O(O));  // open: OP
  CPU_REG_BYTE cpu_reg_byte_42 (
    .H(cpu_decoder_4x16_1_out_11), .V(cpu_decoder_4x16_2_out_15), .S(S), .E(E), .I(I), .RESET(RESET), .O(O));  // open: OP
  CPU_REG_BYTE cpu_reg_byte_43 (
    .H(cpu_decoder_4x16_1_out_12), .V(cpu_decoder_4x16_2_out_15), .S(S), .E(E), .I(I), .RESET(RESET), .O(O));  // open: OP
  CPU_REG_BYTE cpu_reg_byte_44 (
    .H(cpu_decoder_4x16_1_out_13), .V(cpu_decoder_4x16_2_out_15), .S(S), .E(E), .I(I), .RESET(RESET), .O(O));  // open: OP
  CPU_REG_BYTE cpu_reg_byte_45 (
    .H(cpu_decoder_4x16_1_out_14), .V(cpu_decoder_4x16_2_out_15), .S(S), .E(E), .I(I), .RESET(RESET), .O(O));  // open: OP
  CPU_REG_BYTE cpu_reg_byte_46 (
    .H(cpu_decoder_4x16_1_out_15), .V(cpu_decoder_4x16_2_out_15), .S(S), .E(E), .I(I), .RESET(RESET), .O(O));  // open: OP
  CPU_REG_BYTE cpu_reg_byte_47 (
    .H(cpu_decoder_4x16_1_out_16), .V(cpu_decoder_4x16_2_out_15), .S(S), .E(E), .I(I), .RESET(RESET), .O(O));  // open: OP
  CPU_REG_BYTE cpu_reg_byte_48 (
    .H(cpu_decoder_4x16_1_out_17), .V(cpu_decoder_4x16_2_out_15), .S(S), .E(E), .I(I), .RESET(RESET), .O(O));  // open: OP
  CPU_REG_BYTE cpu_reg_byte_49 (
    .H(cpu_decoder_4x16_1_out_2), .V(cpu_decoder_4x16_2_out_14), .S(S), .E(E), .I(I), .RESET(RESET), .O(O));  // open: OP
  CPU_REG_BYTE cpu_reg_byte_50 (
    .H(cpu_decoder_4x16_1_out_3), .V(cpu_decoder_4x16_2_out_14), .S(S), .E(E), .I(I), .RESET(RESET), .O(O));  // open: OP
  CPU_REG_BYTE cpu_reg_byte_51 (
    .H(cpu_decoder_4x16_1_out_4), .V(cpu_decoder_4x16_2_out_14), .S(S), .E(E), .I(I), .RESET(RESET), .O(O));  // open: OP
  CPU_REG_BYTE cpu_reg_byte_52 (
    .H(cpu_decoder_4x16_1_out_5), .V(cpu_decoder_4x16_2_out_14), .S(S), .E(E), .I(I), .RESET(RESET), .O(O));  // open: OP
  CPU_REG_BYTE cpu_reg_byte_53 (
    .H(cpu_decoder_4x16_1_out_6), .V(cpu_decoder_4x16_2_out_14), .S(S), .E(E), .I(I), .RESET(RESET), .O(O));  // open: OP
  CPU_REG_BYTE cpu_reg_byte_54 (
    .H(cpu_decoder_4x16_1_out_7), .V(cpu_decoder_4x16_2_out_14), .S(S), .E(E), .I(I), .RESET(RESET), .O(O));  // open: OP
  CPU_REG_BYTE cpu_reg_byte_55 (
    .H(cpu_decoder_4x16_1_out_8), .V(cpu_decoder_4x16_2_out_14), .S(S), .E(E), .I(I), .RESET(RESET), .O(O));  // open: OP
  CPU_REG_BYTE cpu_reg_byte_56 (
    .H(cpu_decoder_4x16_1_out_9), .V(cpu_decoder_4x16_2_out_14), .S(S), .E(E), .I(I), .RESET(RESET), .O(O));  // open: OP
  CPU_REG_BYTE cpu_reg_byte_57 (
    .H(cpu_decoder_4x16_1_out_10), .V(cpu_decoder_4x16_2_out_14), .S(S), .E(E), .I(I), .RESET(RESET), .O(O));  // open: OP
  CPU_REG_BYTE cpu_reg_byte_58 (
    .H(cpu_decoder_4x16_1_out_11), .V(cpu_decoder_4x16_2_out_14), .S(S), .E(E), .I(I), .RESET(RESET), .O(O));  // open: OP
  CPU_REG_BYTE cpu_reg_byte_59 (
    .H(cpu_decoder_4x16_1_out_12), .V(cpu_decoder_4x16_2_out_14), .S(S), .E(E), .I(I), .RESET(RESET), .O(O));  // open: OP
  CPU_REG_BYTE cpu_reg_byte_60 (
    .H(cpu_decoder_4x16_1_out_13), .V(cpu_decoder_4x16_2_out_14), .S(S), .E(E), .I(I), .RESET(RESET), .O(O));  // open: OP
  CPU_REG_BYTE cpu_reg_byte_61 (
    .H(cpu_decoder_4x16_1_out_14), .V(cpu_decoder_4x16_2_out_14), .S(S), .E(E), .I(I), .RESET(RESET), .O(O));  // open: OP
  CPU_REG_BYTE cpu_reg_byte_62 (
    .H(cpu_decoder_4x16_1_out_15), .V(cpu_decoder_4x16_2_out_14), .S(S), .E(E), .I(I), .RESET(RESET), .O(O));  // open: OP
  CPU_REG_BYTE cpu_reg_byte_63 (
    .H(cpu_decoder_4x16_1_out_16), .V(cpu_decoder_4x16_2_out_14), .S(S), .E(E), .I(I), .RESET(RESET), .O(O));  // open: OP
  CPU_REG_BYTE cpu_reg_byte_64 (
    .H(cpu_decoder_4x16_1_out_17), .V(cpu_decoder_4x16_2_out_14), .S(S), .E(E), .I(I), .RESET(RESET), .O(O));  // open: OP
  CPU_REG_BYTE cpu_reg_byte_65 (
    .H(cpu_decoder_4x16_1_out_2), .V(cpu_decoder_4x16_2_out_13), .S(S), .E(E), .I(I), .RESET(RESET), .O(O));  // open: OP
  CPU_REG_BYTE cpu_reg_byte_66 (
    .H(cpu_decoder_4x16_1_out_3), .V(cpu_decoder_4x16_2_out_13), .S(S), .E(E), .I(I), .RESET(RESET), .O(O));  // open: OP
  CPU_REG_BYTE cpu_reg_byte_67 (
    .H(cpu_decoder_4x16_1_out_4), .V(cpu_decoder_4x16_2_out_13), .S(S), .E(E), .I(I), .RESET(RESET), .O(O));  // open: OP
  CPU_REG_BYTE cpu_reg_byte_68 (
    .H(cpu_decoder_4x16_1_out_5), .V(cpu_decoder_4x16_2_out_13), .S(S), .E(E), .I(I), .RESET(RESET), .O(O));  // open: OP
  CPU_REG_BYTE cpu_reg_byte_69 (
    .H(cpu_decoder_4x16_1_out_6), .V(cpu_decoder_4x16_2_out_13), .S(S), .E(E), .I(I), .RESET(RESET), .O(O));  // open: OP
  CPU_REG_BYTE cpu_reg_byte_70 (
    .H(cpu_decoder_4x16_1_out_7), .V(cpu_decoder_4x16_2_out_13), .S(S), .E(E), .I(I), .RESET(RESET), .O(O));  // open: OP
  CPU_REG_BYTE cpu_reg_byte_71 (
    .H(cpu_decoder_4x16_1_out_8), .V(cpu_decoder_4x16_2_out_13), .S(S), .E(E), .I(I), .RESET(RESET), .O(O));  // open: OP
  CPU_REG_BYTE cpu_reg_byte_72 (
    .H(cpu_decoder_4x16_1_out_9), .V(cpu_decoder_4x16_2_out_13), .S(S), .E(E), .I(I), .RESET(RESET), .O(O));  // open: OP
  CPU_REG_BYTE cpu_reg_byte_73 (
    .H(cpu_decoder_4x16_1_out_10), .V(cpu_decoder_4x16_2_out_13), .S(S), .E(E), .I(I), .RESET(RESET), .O(O));  // open: OP
  CPU_REG_BYTE cpu_reg_byte_74 (
    .H(cpu_decoder_4x16_1_out_11), .V(cpu_decoder_4x16_2_out_13), .S(S), .E(E), .I(I), .RESET(RESET), .O(O));  // open: OP
  CPU_REG_BYTE cpu_reg_byte_75 (
    .H(cpu_decoder_4x16_1_out_12), .V(cpu_decoder_4x16_2_out_13), .S(S), .E(E), .I(I), .RESET(RESET), .O(O));  // open: OP
  CPU_REG_BYTE cpu_reg_byte_76 (
    .H(cpu_decoder_4x16_1_out_13), .V(cpu_decoder_4x16_2_out_13), .S(S), .E(E), .I(I), .RESET(RESET), .O(O));  // open: OP
  CPU_REG_BYTE cpu_reg_byte_77 (
    .H(cpu_decoder_4x16_1_out_14), .V(cpu_decoder_4x16_2_out_13), .S(S), .E(E), .I(I), .RESET(RESET), .O(O));  // open: OP
  CPU_REG_BYTE cpu_reg_byte_78 (
    .H(cpu_decoder_4x16_1_out_15), .V(cpu_decoder_4x16_2_out_13), .S(S), .E(E), .I(I), .RESET(RESET), .O(O));  // open: OP
  CPU_REG_BYTE cpu_reg_byte_79 (
    .H(cpu_decoder_4x16_1_out_16), .V(cpu_decoder_4x16_2_out_13), .S(S), .E(E), .I(I), .RESET(RESET), .O(O));  // open: OP
  CPU_REG_BYTE cpu_reg_byte_80 (
    .H(cpu_decoder_4x16_1_out_17), .V(cpu_decoder_4x16_2_out_13), .S(S), .E(E), .I(I), .RESET(RESET), .O(O));  // open: OP
  CPU_REG_BYTE cpu_reg_byte_81 (
    .H(cpu_decoder_4x16_1_out_2), .V(cpu_decoder_4x16_2_out_12), .S(S), .E(E), .I(I), .RESET(RESET), .O(O));  // open: OP
  CPU_REG_BYTE cpu_reg_byte_82 (
    .H(cpu_decoder_4x16_1_out_3), .V(cpu_decoder_4x16_2_out_12), .S(S), .E(E), .I(I), .RESET(RESET), .O(O));  // open: OP
  CPU_REG_BYTE cpu_reg_byte_83 (
    .H(cpu_decoder_4x16_1_out_4), .V(cpu_decoder_4x16_2_out_12), .S(S), .E(E), .I(I), .RESET(RESET), .O(O));  // open: OP
  CPU_REG_BYTE cpu_reg_byte_84 (
    .H(cpu_decoder_4x16_1_out_5), .V(cpu_decoder_4x16_2_out_12), .S(S), .E(E), .I(I), .RESET(RESET), .O(O));  // open: OP
  CPU_REG_BYTE cpu_reg_byte_85 (
    .H(cpu_decoder_4x16_1_out_6), .V(cpu_decoder_4x16_2_out_12), .S(S), .E(E), .I(I), .RESET(RESET), .O(O));  // open: OP
  CPU_REG_BYTE cpu_reg_byte_86 (
    .H(cpu_decoder_4x16_1_out_7), .V(cpu_decoder_4x16_2_out_12), .S(S), .E(E), .I(I), .RESET(RESET), .O(O));  // open: OP
  CPU_REG_BYTE cpu_reg_byte_87 (
    .H(cpu_decoder_4x16_1_out_8), .V(cpu_decoder_4x16_2_out_12), .S(S), .E(E), .I(I), .RESET(RESET), .O(O));  // open: OP
  CPU_REG_BYTE cpu_reg_byte_88 (
    .H(cpu_decoder_4x16_1_out_9), .V(cpu_decoder_4x16_2_out_12), .S(S), .E(E), .I(I), .RESET(RESET), .O(O));  // open: OP
  CPU_REG_BYTE cpu_reg_byte_89 (
    .H(cpu_decoder_4x16_1_out_10), .V(cpu_decoder_4x16_2_out_12), .S(S), .E(E), .I(I), .RESET(RESET), .O(O));  // open: OP
  CPU_REG_BYTE cpu_reg_byte_90 (
    .H(cpu_decoder_4x16_1_out_11), .V(cpu_decoder_4x16_2_out_12), .S(S), .E(E), .I(I), .RESET(RESET), .O(O));  // open: OP
  CPU_REG_BYTE cpu_reg_byte_91 (
    .H(cpu_decoder_4x16_1_out_12), .V(cpu_decoder_4x16_2_out_12), .S(S), .E(E), .I(I), .RESET(RESET), .O(O));  // open: OP
  CPU_REG_BYTE cpu_reg_byte_92 (
    .H(cpu_decoder_4x16_1_out_13), .V(cpu_decoder_4x16_2_out_12), .S(S), .E(E), .I(I), .RESET(RESET), .O(O));  // open: OP
  CPU_REG_BYTE cpu_reg_byte_93 (
    .H(cpu_decoder_4x16_1_out_14), .V(cpu_decoder_4x16_2_out_12), .S(S), .E(E), .I(I), .RESET(RESET), .O(O));  // open: OP
  CPU_REG_BYTE cpu_reg_byte_94 (
    .H(cpu_decoder_4x16_1_out_15), .V(cpu_decoder_4x16_2_out_12), .S(S), .E(E), .I(I), .RESET(RESET), .O(O));  // open: OP
  CPU_REG_BYTE cpu_reg_byte_95 (
    .H(cpu_decoder_4x16_1_out_16), .V(cpu_decoder_4x16_2_out_12), .S(S), .E(E), .I(I), .RESET(RESET), .O(O));  // open: OP
  CPU_REG_BYTE cpu_reg_byte_96 (
    .H(cpu_decoder_4x16_1_out_17), .V(cpu_decoder_4x16_2_out_12), .S(S), .E(E), .I(I), .RESET(RESET), .O(O));  // open: OP
  CPU_REG_BYTE cpu_reg_byte_97 (
    .H(cpu_decoder_4x16_1_out_2), .V(cpu_decoder_4x16_2_out_11), .S(S), .E(E), .I(I), .RESET(RESET), .O(O));  // open: OP
  CPU_REG_BYTE cpu_reg_byte_98 (
    .H(cpu_decoder_4x16_1_out_3), .V(cpu_decoder_4x16_2_out_11), .S(S), .E(E), .I(I), .RESET(RESET), .O(O));  // open: OP
  CPU_REG_BYTE cpu_reg_byte_99 (
    .H(cpu_decoder_4x16_1_out_4), .V(cpu_decoder_4x16_2_out_11), .S(S), .E(E), .I(I), .RESET(RESET), .O(O));  // open: OP
  CPU_REG_BYTE cpu_reg_byte_100 (
    .H(cpu_decoder_4x16_1_out_5), .V(cpu_decoder_4x16_2_out_11), .S(S), .E(E), .I(I), .RESET(RESET), .O(O));  // open: OP
  CPU_REG_BYTE cpu_reg_byte_101 (
    .H(cpu_decoder_4x16_1_out_6), .V(cpu_decoder_4x16_2_out_11), .S(S), .E(E), .I(I), .RESET(RESET), .O(O));  // open: OP
  CPU_REG_BYTE cpu_reg_byte_102 (
    .H(cpu_decoder_4x16_1_out_7), .V(cpu_decoder_4x16_2_out_11), .S(S), .E(E), .I(I), .RESET(RESET), .O(O));  // open: OP
  CPU_REG_BYTE cpu_reg_byte_103 (
    .H(cpu_decoder_4x16_1_out_8), .V(cpu_decoder_4x16_2_out_11), .S(S), .E(E), .I(I), .RESET(RESET), .O(O));  // open: OP
  CPU_REG_BYTE cpu_reg_byte_104 (
    .H(cpu_decoder_4x16_1_out_9), .V(cpu_decoder_4x16_2_out_11), .S(S), .E(E), .I(I), .RESET(RESET), .O(O));  // open: OP
  CPU_REG_BYTE cpu_reg_byte_105 (
    .H(cpu_decoder_4x16_1_out_10), .V(cpu_decoder_4x16_2_out_11), .S(S), .E(E), .I(I), .RESET(RESET), .O(O));  // open: OP
  CPU_REG_BYTE cpu_reg_byte_106 (
    .H(cpu_decoder_4x16_1_out_11), .V(cpu_decoder_4x16_2_out_11), .S(S), .E(E), .I(I), .RESET(RESET), .O(O));  // open: OP
  CPU_REG_BYTE cpu_reg_byte_107 (
    .H(cpu_decoder_4x16_1_out_12), .V(cpu_decoder_4x16_2_out_11), .S(S), .E(E), .I(I), .RESET(RESET), .O(O));  // open: OP
  CPU_REG_BYTE cpu_reg_byte_108 (
    .H(cpu_decoder_4x16_1_out_13), .V(cpu_decoder_4x16_2_out_11), .S(S), .E(E), .I(I), .RESET(RESET), .O(O));  // open: OP
  CPU_REG_BYTE cpu_reg_byte_109 (
    .H(cpu_decoder_4x16_1_out_14), .V(cpu_decoder_4x16_2_out_11), .S(S), .E(E), .I(I), .RESET(RESET), .O(O));  // open: OP
  CPU_REG_BYTE cpu_reg_byte_110 (
    .H(cpu_decoder_4x16_1_out_15), .V(cpu_decoder_4x16_2_out_11), .S(S), .E(E), .I(I), .RESET(RESET), .O(O));  // open: OP
  CPU_REG_BYTE cpu_reg_byte_111 (
    .H(cpu_decoder_4x16_1_out_16), .V(cpu_decoder_4x16_2_out_11), .S(S), .E(E), .I(I), .RESET(RESET), .O(O));  // open: OP
  CPU_REG_BYTE cpu_reg_byte_112 (
    .H(cpu_decoder_4x16_1_out_17), .V(cpu_decoder_4x16_2_out_11), .S(S), .E(E), .I(I), .RESET(RESET), .O(O));  // open: OP
  CPU_REG_BYTE cpu_reg_byte_113 (
    .H(cpu_decoder_4x16_1_out_2), .V(cpu_decoder_4x16_2_out_10), .S(S), .E(E), .I(I), .RESET(RESET), .O(O));  // open: OP
  CPU_REG_BYTE cpu_reg_byte_114 (
    .H(cpu_decoder_4x16_1_out_3), .V(cpu_decoder_4x16_2_out_10), .S(S), .E(E), .I(I), .RESET(RESET), .O(O));  // open: OP
  CPU_REG_BYTE cpu_reg_byte_115 (
    .H(cpu_decoder_4x16_1_out_4), .V(cpu_decoder_4x16_2_out_10), .S(S), .E(E), .I(I), .RESET(RESET), .O(O));  // open: OP
  CPU_REG_BYTE cpu_reg_byte_116 (
    .H(cpu_decoder_4x16_1_out_5), .V(cpu_decoder_4x16_2_out_10), .S(S), .E(E), .I(I), .RESET(RESET), .O(O));  // open: OP
  CPU_REG_BYTE cpu_reg_byte_117 (
    .H(cpu_decoder_4x16_1_out_6), .V(cpu_decoder_4x16_2_out_10), .S(S), .E(E), .I(I), .RESET(RESET), .O(O));  // open: OP
  CPU_REG_BYTE cpu_reg_byte_118 (
    .H(cpu_decoder_4x16_1_out_7), .V(cpu_decoder_4x16_2_out_10), .S(S), .E(E), .I(I), .RESET(RESET), .O(O));  // open: OP
  CPU_REG_BYTE cpu_reg_byte_119 (
    .H(cpu_decoder_4x16_1_out_8), .V(cpu_decoder_4x16_2_out_10), .S(S), .E(E), .I(I), .RESET(RESET), .O(O));  // open: OP
  CPU_REG_BYTE cpu_reg_byte_120 (
    .H(cpu_decoder_4x16_1_out_9), .V(cpu_decoder_4x16_2_out_10), .S(S), .E(E), .I(I), .RESET(RESET), .O(O));  // open: OP
  CPU_REG_BYTE cpu_reg_byte_121 (
    .H(cpu_decoder_4x16_1_out_10), .V(cpu_decoder_4x16_2_out_10), .S(S), .E(E), .I(I), .RESET(RESET), .O(O));  // open: OP
  CPU_REG_BYTE cpu_reg_byte_122 (
    .H(cpu_decoder_4x16_1_out_11), .V(cpu_decoder_4x16_2_out_10), .S(S), .E(E), .I(I), .RESET(RESET), .O(O));  // open: OP
  CPU_REG_BYTE cpu_reg_byte_123 (
    .H(cpu_decoder_4x16_1_out_12), .V(cpu_decoder_4x16_2_out_10), .S(S), .E(E), .I(I), .RESET(RESET), .O(O));  // open: OP
  CPU_REG_BYTE cpu_reg_byte_124 (
    .H(cpu_decoder_4x16_1_out_13), .V(cpu_decoder_4x16_2_out_10), .S(S), .E(E), .I(I), .RESET(RESET), .O(O));  // open: OP
  CPU_REG_BYTE cpu_reg_byte_125 (
    .H(cpu_decoder_4x16_1_out_14), .V(cpu_decoder_4x16_2_out_10), .S(S), .E(E), .I(I), .RESET(RESET), .O(O));  // open: OP
  CPU_REG_BYTE cpu_reg_byte_126 (
    .H(cpu_decoder_4x16_1_out_15), .V(cpu_decoder_4x16_2_out_10), .S(S), .E(E), .I(I), .RESET(RESET), .O(O));  // open: OP
  CPU_REG_BYTE cpu_reg_byte_127 (
    .H(cpu_decoder_4x16_1_out_16), .V(cpu_decoder_4x16_2_out_10), .S(S), .E(E), .I(I), .RESET(RESET), .O(O));  // open: OP
  CPU_REG_BYTE cpu_reg_byte_128 (
    .H(cpu_decoder_4x16_1_out_17), .V(cpu_decoder_4x16_2_out_10), .S(S), .E(E), .I(I), .RESET(RESET), .O(O));  // open: OP
  CPU_DECODER_4x16 cpu_decoder_4x16_2 (
    .I(cpu_mem_8_bit_1_o[3:0]), .out_13(cpu_decoder_4x16_2_out_13), .out_14(cpu_decoder_4x16_2_out_14),
    .out_15(cpu_decoder_4x16_2_out_15), .out_16(cpu_decoder_4x16_2_out_16),
    .out_17(cpu_decoder_4x16_2_out_17), .out_2(cpu_decoder_4x16_2_out_2), .out_3(cpu_decoder_4x16_2_out_3),
    .out_4(cpu_decoder_4x16_2_out_4), .out_5(cpu_decoder_4x16_2_out_5), .out_6(cpu_decoder_4x16_2_out_6),
    .out_7(cpu_decoder_4x16_2_out_7), .out_8(cpu_decoder_4x16_2_out_8), .out_9(cpu_decoder_4x16_2_out_9),
    .out_10(cpu_decoder_4x16_2_out_10), .out_11(cpu_decoder_4x16_2_out_11), .out_12(cpu_decoder_4x16_2_out_12));
  CPU_REG_BYTE cpu_reg_byte_129 (
    .H(cpu_decoder_4x16_1_out_2), .V(cpu_decoder_4x16_2_out_9), .S(S), .E(E), .I(I), .RESET(RESET), .O(O));  // open: OP
  CPU_REG_BYTE cpu_reg_byte_130 (
    .H(cpu_decoder_4x16_1_out_3), .V(cpu_decoder_4x16_2_out_9), .S(S), .E(E), .I(I), .RESET(RESET), .O(O));  // open: OP
  CPU_REG_BYTE cpu_reg_byte_131 (
    .H(cpu_decoder_4x16_1_out_4), .V(cpu_decoder_4x16_2_out_9), .S(S), .E(E), .I(I), .RESET(RESET), .O(O));  // open: OP
  CPU_REG_BYTE cpu_reg_byte_132 (
    .H(cpu_decoder_4x16_1_out_5), .V(cpu_decoder_4x16_2_out_9), .S(S), .E(E), .I(I), .RESET(RESET), .O(O));  // open: OP
  CPU_REG_BYTE cpu_reg_byte_133 (
    .H(cpu_decoder_4x16_1_out_6), .V(cpu_decoder_4x16_2_out_9), .S(S), .E(E), .I(I), .RESET(RESET), .O(O));  // open: OP
  CPU_REG_BYTE cpu_reg_byte_134 (
    .H(cpu_decoder_4x16_1_out_7), .V(cpu_decoder_4x16_2_out_9), .S(S), .E(E), .I(I), .RESET(RESET), .O(O));  // open: OP
  CPU_REG_BYTE cpu_reg_byte_135 (
    .H(cpu_decoder_4x16_1_out_8), .V(cpu_decoder_4x16_2_out_9), .S(S), .E(E), .I(I), .RESET(RESET), .O(O));  // open: OP
  CPU_REG_BYTE cpu_reg_byte_136 (
    .H(cpu_decoder_4x16_1_out_9), .V(cpu_decoder_4x16_2_out_9), .S(S), .E(E), .I(I), .RESET(RESET), .O(O));  // open: OP
  CPU_REG_BYTE cpu_reg_byte_137 (
    .H(cpu_decoder_4x16_1_out_10), .V(cpu_decoder_4x16_2_out_9), .S(S), .E(E), .I(I), .RESET(RESET), .O(O));  // open: OP
  CPU_REG_BYTE cpu_reg_byte_138 (
    .H(cpu_decoder_4x16_1_out_11), .V(cpu_decoder_4x16_2_out_9), .S(S), .E(E), .I(I), .RESET(RESET), .O(O));  // open: OP
  CPU_REG_BYTE cpu_reg_byte_139 (
    .H(cpu_decoder_4x16_1_out_12), .V(cpu_decoder_4x16_2_out_9), .S(S), .E(E), .I(I), .RESET(RESET), .O(O));  // open: OP
  CPU_REG_BYTE cpu_reg_byte_140 (
    .H(cpu_decoder_4x16_1_out_13), .V(cpu_decoder_4x16_2_out_9), .S(S), .E(E), .I(I), .RESET(RESET), .O(O));  // open: OP
  CPU_REG_BYTE cpu_reg_byte_141 (
    .H(cpu_decoder_4x16_1_out_14), .V(cpu_decoder_4x16_2_out_9), .S(S), .E(E), .I(I), .RESET(RESET), .O(O));  // open: OP
  CPU_REG_BYTE cpu_reg_byte_142 (
    .H(cpu_decoder_4x16_1_out_15), .V(cpu_decoder_4x16_2_out_9), .S(S), .E(E), .I(I), .RESET(RESET), .O(O));  // open: OP
  CPU_REG_BYTE cpu_reg_byte_143 (
    .H(cpu_decoder_4x16_1_out_16), .V(cpu_decoder_4x16_2_out_9), .S(S), .E(E), .I(I), .RESET(RESET), .O(O));  // open: OP
  CPU_REG_BYTE cpu_reg_byte_144 (
    .H(cpu_decoder_4x16_1_out_17), .V(cpu_decoder_4x16_2_out_9), .S(S), .E(E), .I(I), .RESET(RESET), .O(O));  // open: OP
  CPU_REG_BYTE cpu_reg_byte_145 (
    .H(cpu_decoder_4x16_1_out_2), .V(cpu_decoder_4x16_2_out_8), .S(S), .E(E), .I(I), .RESET(RESET), .O(O));  // open: OP
  CPU_REG_BYTE cpu_reg_byte_146 (
    .H(cpu_decoder_4x16_1_out_3), .V(cpu_decoder_4x16_2_out_8), .S(S), .E(E), .I(I), .RESET(RESET), .O(O));  // open: OP
  CPU_REG_BYTE cpu_reg_byte_147 (
    .H(cpu_decoder_4x16_1_out_4), .V(cpu_decoder_4x16_2_out_8), .S(S), .E(E), .I(I), .RESET(RESET), .O(O));  // open: OP
  CPU_REG_BYTE cpu_reg_byte_148 (
    .H(cpu_decoder_4x16_1_out_5), .V(cpu_decoder_4x16_2_out_8), .S(S), .E(E), .I(I), .RESET(RESET), .O(O));  // open: OP
  CPU_REG_BYTE cpu_reg_byte_149 (
    .H(cpu_decoder_4x16_1_out_6), .V(cpu_decoder_4x16_2_out_8), .S(S), .E(E), .I(I), .RESET(RESET), .O(O));  // open: OP
  CPU_REG_BYTE cpu_reg_byte_150 (
    .H(cpu_decoder_4x16_1_out_7), .V(cpu_decoder_4x16_2_out_8), .S(S), .E(E), .I(I), .RESET(RESET), .O(O));  // open: OP
  CPU_REG_BYTE cpu_reg_byte_151 (
    .H(cpu_decoder_4x16_1_out_8), .V(cpu_decoder_4x16_2_out_8), .S(S), .E(E), .I(I), .RESET(RESET), .O(O));  // open: OP
  CPU_REG_BYTE cpu_reg_byte_152 (
    .H(cpu_decoder_4x16_1_out_9), .V(cpu_decoder_4x16_2_out_8), .S(S), .E(E), .I(I), .RESET(RESET), .O(O));  // open: OP
  CPU_REG_BYTE cpu_reg_byte_153 (
    .H(cpu_decoder_4x16_1_out_10), .V(cpu_decoder_4x16_2_out_8), .S(S), .E(E), .I(I), .RESET(RESET), .O(O));  // open: OP
  CPU_REG_BYTE cpu_reg_byte_154 (
    .H(cpu_decoder_4x16_1_out_11), .V(cpu_decoder_4x16_2_out_8), .S(S), .E(E), .I(I), .RESET(RESET), .O(O));  // open: OP
  CPU_REG_BYTE cpu_reg_byte_155 (
    .H(cpu_decoder_4x16_1_out_12), .V(cpu_decoder_4x16_2_out_8), .S(S), .E(E), .I(I), .RESET(RESET), .O(O));  // open: OP
  CPU_REG_BYTE cpu_reg_byte_156 (
    .H(cpu_decoder_4x16_1_out_13), .V(cpu_decoder_4x16_2_out_8), .S(S), .E(E), .I(I), .RESET(RESET), .O(O));  // open: OP
  CPU_REG_BYTE cpu_reg_byte_157 (
    .H(cpu_decoder_4x16_1_out_14), .V(cpu_decoder_4x16_2_out_8), .S(S), .E(E), .I(I), .RESET(RESET), .O(O));  // open: OP
  CPU_REG_BYTE cpu_reg_byte_158 (
    .H(cpu_decoder_4x16_1_out_15), .V(cpu_decoder_4x16_2_out_8), .S(S), .E(E), .I(I), .RESET(RESET), .O(O));  // open: OP
  CPU_REG_BYTE cpu_reg_byte_159 (
    .H(cpu_decoder_4x16_1_out_16), .V(cpu_decoder_4x16_2_out_8), .S(S), .E(E), .I(I), .RESET(RESET), .O(O));  // open: OP
  CPU_REG_BYTE cpu_reg_byte_160 (
    .H(cpu_decoder_4x16_1_out_17), .V(cpu_decoder_4x16_2_out_8), .S(S), .E(E), .I(I), .RESET(RESET), .O(O));  // open: OP
  CPU_REG_BYTE cpu_reg_byte_161 (
    .H(cpu_decoder_4x16_1_out_2), .V(cpu_decoder_4x16_2_out_7), .S(S), .E(E), .I(I), .RESET(RESET), .O(O));  // open: OP
  CPU_REG_BYTE cpu_reg_byte_162 (
    .H(cpu_decoder_4x16_1_out_3), .V(cpu_decoder_4x16_2_out_7), .S(S), .E(E), .I(I), .RESET(RESET), .O(O));  // open: OP
  CPU_REG_BYTE cpu_reg_byte_163 (
    .H(cpu_decoder_4x16_1_out_4), .V(cpu_decoder_4x16_2_out_7), .S(S), .E(E), .I(I), .RESET(RESET), .O(O));  // open: OP
  CPU_REG_BYTE cpu_reg_byte_164 (
    .H(cpu_decoder_4x16_1_out_5), .V(cpu_decoder_4x16_2_out_7), .S(S), .E(E), .I(I), .RESET(RESET), .O(O));  // open: OP
  CPU_REG_BYTE cpu_reg_byte_165 (
    .H(cpu_decoder_4x16_1_out_6), .V(cpu_decoder_4x16_2_out_7), .S(S), .E(E), .I(I), .RESET(RESET), .O(O));  // open: OP
  CPU_REG_BYTE cpu_reg_byte_166 (
    .H(cpu_decoder_4x16_1_out_7), .V(cpu_decoder_4x16_2_out_7), .S(S), .E(E), .I(I), .RESET(RESET), .O(O));  // open: OP
  CPU_REG_BYTE cpu_reg_byte_167 (
    .H(cpu_decoder_4x16_1_out_8), .V(cpu_decoder_4x16_2_out_7), .S(S), .E(E), .I(I), .RESET(RESET), .O(O));  // open: OP
  CPU_REG_BYTE cpu_reg_byte_168 (
    .H(cpu_decoder_4x16_1_out_9), .V(cpu_decoder_4x16_2_out_7), .S(S), .E(E), .I(I), .RESET(RESET), .O(O));  // open: OP
  CPU_REG_BYTE cpu_reg_byte_169 (
    .H(cpu_decoder_4x16_1_out_10), .V(cpu_decoder_4x16_2_out_7), .S(S), .E(E), .I(I), .RESET(RESET), .O(O));  // open: OP
  CPU_REG_BYTE cpu_reg_byte_170 (
    .H(cpu_decoder_4x16_1_out_11), .V(cpu_decoder_4x16_2_out_7), .S(S), .E(E), .I(I), .RESET(RESET), .O(O));  // open: OP
  CPU_REG_BYTE cpu_reg_byte_171 (
    .H(cpu_decoder_4x16_1_out_12), .V(cpu_decoder_4x16_2_out_7), .S(S), .E(E), .I(I), .RESET(RESET), .O(O));  // open: OP
  CPU_REG_BYTE cpu_reg_byte_172 (
    .H(cpu_decoder_4x16_1_out_13), .V(cpu_decoder_4x16_2_out_7), .S(S), .E(E), .I(I), .RESET(RESET), .O(O));  // open: OP
  CPU_REG_BYTE cpu_reg_byte_173 (
    .H(cpu_decoder_4x16_1_out_14), .V(cpu_decoder_4x16_2_out_7), .S(S), .E(E), .I(I), .RESET(RESET), .O(O));  // open: OP
  CPU_REG_BYTE cpu_reg_byte_174 (
    .H(cpu_decoder_4x16_1_out_15), .V(cpu_decoder_4x16_2_out_7), .S(S), .E(E), .I(I), .RESET(RESET), .O(O));  // open: OP
  CPU_REG_BYTE cpu_reg_byte_175 (
    .H(cpu_decoder_4x16_1_out_16), .V(cpu_decoder_4x16_2_out_7), .S(S), .E(E), .I(I), .RESET(RESET), .O(O));  // open: OP
  CPU_REG_BYTE cpu_reg_byte_176 (
    .H(cpu_decoder_4x16_1_out_17), .V(cpu_decoder_4x16_2_out_7), .S(S), .E(E), .I(I), .RESET(RESET), .O(O));  // open: OP
  CPU_REG_BYTE cpu_reg_byte_177 (
    .H(cpu_decoder_4x16_1_out_2), .V(cpu_decoder_4x16_2_out_6), .S(S), .E(E), .I(I), .RESET(RESET), .O(O));  // open: OP
  CPU_REG_BYTE cpu_reg_byte_178 (
    .H(cpu_decoder_4x16_1_out_3), .V(cpu_decoder_4x16_2_out_6), .S(S), .E(E), .I(I), .RESET(RESET), .O(O));  // open: OP
  CPU_REG_BYTE cpu_reg_byte_179 (
    .H(cpu_decoder_4x16_1_out_4), .V(cpu_decoder_4x16_2_out_6), .S(S), .E(E), .I(I), .RESET(RESET), .O(O));  // open: OP
  CPU_REG_BYTE cpu_reg_byte_180 (
    .H(cpu_decoder_4x16_1_out_5), .V(cpu_decoder_4x16_2_out_6), .S(S), .E(E), .I(I), .RESET(RESET), .O(O));  // open: OP
  CPU_REG_BYTE cpu_reg_byte_181 (
    .H(cpu_decoder_4x16_1_out_6), .V(cpu_decoder_4x16_2_out_6), .S(S), .E(E), .I(I), .RESET(RESET), .O(O));  // open: OP
  CPU_REG_BYTE cpu_reg_byte_182 (
    .H(cpu_decoder_4x16_1_out_7), .V(cpu_decoder_4x16_2_out_6), .S(S), .E(E), .I(I), .RESET(RESET), .O(O));  // open: OP
  CPU_REG_BYTE cpu_reg_byte_183 (
    .H(cpu_decoder_4x16_1_out_8), .V(cpu_decoder_4x16_2_out_6), .S(S), .E(E), .I(I), .RESET(RESET), .O(O));  // open: OP
  CPU_REG_BYTE cpu_reg_byte_184 (
    .H(cpu_decoder_4x16_1_out_9), .V(cpu_decoder_4x16_2_out_6), .S(S), .E(E), .I(I), .RESET(RESET), .O(O));  // open: OP
  CPU_REG_BYTE cpu_reg_byte_185 (
    .H(cpu_decoder_4x16_1_out_10), .V(cpu_decoder_4x16_2_out_6), .S(S), .E(E), .I(I), .RESET(RESET), .O(O));  // open: OP
  CPU_REG_BYTE cpu_reg_byte_186 (
    .H(cpu_decoder_4x16_1_out_11), .V(cpu_decoder_4x16_2_out_6), .S(S), .E(E), .I(I), .RESET(RESET), .O(O));  // open: OP
  CPU_REG_BYTE cpu_reg_byte_187 (
    .H(cpu_decoder_4x16_1_out_12), .V(cpu_decoder_4x16_2_out_6), .S(S), .E(E), .I(I), .RESET(RESET), .O(O));  // open: OP
  CPU_REG_BYTE cpu_reg_byte_188 (
    .H(cpu_decoder_4x16_1_out_13), .V(cpu_decoder_4x16_2_out_6), .S(S), .E(E), .I(I), .RESET(RESET), .O(O));  // open: OP
  CPU_REG_BYTE cpu_reg_byte_189 (
    .H(cpu_decoder_4x16_1_out_14), .V(cpu_decoder_4x16_2_out_6), .S(S), .E(E), .I(I), .RESET(RESET), .O(O));  // open: OP
  CPU_REG_BYTE cpu_reg_byte_190 (
    .H(cpu_decoder_4x16_1_out_15), .V(cpu_decoder_4x16_2_out_6), .S(S), .E(E), .I(I), .RESET(RESET), .O(O));  // open: OP
  CPU_REG_BYTE cpu_reg_byte_191 (
    .H(cpu_decoder_4x16_1_out_16), .V(cpu_decoder_4x16_2_out_6), .S(S), .E(E), .I(I), .RESET(RESET), .O(O));  // open: OP
  CPU_REG_BYTE cpu_reg_byte_192 (
    .H(cpu_decoder_4x16_1_out_17), .V(cpu_decoder_4x16_2_out_6), .S(S), .E(E), .I(I), .RESET(RESET), .O(O));  // open: OP
  CPU_REG_BYTE cpu_reg_byte_193 (
    .H(cpu_decoder_4x16_1_out_2), .V(cpu_decoder_4x16_2_out_5), .S(S), .E(E), .I(I), .RESET(RESET), .O(O));  // open: OP
  CPU_REG_BYTE cpu_reg_byte_194 (
    .H(cpu_decoder_4x16_1_out_3), .V(cpu_decoder_4x16_2_out_5), .S(S), .E(E), .I(I), .RESET(RESET), .O(O));  // open: OP
  CPU_REG_BYTE cpu_reg_byte_195 (
    .H(cpu_decoder_4x16_1_out_4), .V(cpu_decoder_4x16_2_out_5), .S(S), .E(E), .I(I), .RESET(RESET), .O(O));  // open: OP
  CPU_REG_BYTE cpu_reg_byte_196 (
    .H(cpu_decoder_4x16_1_out_5), .V(cpu_decoder_4x16_2_out_5), .S(S), .E(E), .I(I), .RESET(RESET), .O(O));  // open: OP
  CPU_REG_BYTE cpu_reg_byte_197 (
    .H(cpu_decoder_4x16_1_out_6), .V(cpu_decoder_4x16_2_out_5), .S(S), .E(E), .I(I), .RESET(RESET), .O(O));  // open: OP
  CPU_REG_BYTE cpu_reg_byte_198 (
    .H(cpu_decoder_4x16_1_out_7), .V(cpu_decoder_4x16_2_out_5), .S(S), .E(E), .I(I), .RESET(RESET), .O(O));  // open: OP
  CPU_REG_BYTE cpu_reg_byte_199 (
    .H(cpu_decoder_4x16_1_out_8), .V(cpu_decoder_4x16_2_out_5), .S(S), .E(E), .I(I), .RESET(RESET), .O(O));  // open: OP
  CPU_REG_BYTE cpu_reg_byte_200 (
    .H(cpu_decoder_4x16_1_out_9), .V(cpu_decoder_4x16_2_out_5), .S(S), .E(E), .I(I), .RESET(RESET), .O(O));  // open: OP
  CPU_REG_BYTE cpu_reg_byte_201 (
    .H(cpu_decoder_4x16_1_out_10), .V(cpu_decoder_4x16_2_out_5), .S(S), .E(E), .I(I), .RESET(RESET), .O(O));  // open: OP
  CPU_REG_BYTE cpu_reg_byte_202 (
    .H(cpu_decoder_4x16_1_out_11), .V(cpu_decoder_4x16_2_out_5), .S(S), .E(E), .I(I), .RESET(RESET), .O(O));  // open: OP
  CPU_REG_BYTE cpu_reg_byte_203 (
    .H(cpu_decoder_4x16_1_out_12), .V(cpu_decoder_4x16_2_out_5), .S(S), .E(E), .I(I), .RESET(RESET), .O(O));  // open: OP
  CPU_REG_BYTE cpu_reg_byte_204 (
    .H(cpu_decoder_4x16_1_out_13), .V(cpu_decoder_4x16_2_out_5), .S(S), .E(E), .I(I), .RESET(RESET), .O(O));  // open: OP
  CPU_REG_BYTE cpu_reg_byte_205 (
    .H(cpu_decoder_4x16_1_out_14), .V(cpu_decoder_4x16_2_out_5), .S(S), .E(E), .I(I), .RESET(RESET), .O(O));  // open: OP
  CPU_REG_BYTE cpu_reg_byte_206 (
    .H(cpu_decoder_4x16_1_out_15), .V(cpu_decoder_4x16_2_out_5), .S(S), .E(E), .I(I), .RESET(RESET), .O(O));  // open: OP
  CPU_REG_BYTE cpu_reg_byte_207 (
    .H(cpu_decoder_4x16_1_out_16), .V(cpu_decoder_4x16_2_out_5), .S(S), .E(E), .I(I), .RESET(RESET), .O(O));  // open: OP
  CPU_REG_BYTE cpu_reg_byte_208 (
    .H(cpu_decoder_4x16_1_out_17), .V(cpu_decoder_4x16_2_out_5), .S(S), .E(E), .I(I), .RESET(RESET), .O(O));  // open: OP
  CPU_REG_BYTE cpu_reg_byte_209 (
    .H(cpu_decoder_4x16_1_out_2), .V(cpu_decoder_4x16_2_out_4), .S(S), .E(E), .I(I), .RESET(RESET), .O(O));  // open: OP
  CPU_REG_BYTE cpu_reg_byte_210 (
    .H(cpu_decoder_4x16_1_out_3), .V(cpu_decoder_4x16_2_out_4), .S(S), .E(E), .I(I), .RESET(RESET), .O(O));  // open: OP
  CPU_REG_BYTE cpu_reg_byte_211 (
    .H(cpu_decoder_4x16_1_out_4), .V(cpu_decoder_4x16_2_out_4), .S(S), .E(E), .I(I), .RESET(RESET), .O(O));  // open: OP
  CPU_REG_BYTE cpu_reg_byte_212 (
    .H(cpu_decoder_4x16_1_out_5), .V(cpu_decoder_4x16_2_out_4), .S(S), .E(E), .I(I), .RESET(RESET), .O(O));  // open: OP
  CPU_REG_BYTE cpu_reg_byte_213 (
    .H(cpu_decoder_4x16_1_out_6), .V(cpu_decoder_4x16_2_out_4), .S(S), .E(E), .I(I), .RESET(RESET), .O(O));  // open: OP
  CPU_REG_BYTE cpu_reg_byte_214 (
    .H(cpu_decoder_4x16_1_out_7), .V(cpu_decoder_4x16_2_out_4), .S(S), .E(E), .I(I), .RESET(RESET), .O(O));  // open: OP
  CPU_REG_BYTE cpu_reg_byte_215 (
    .H(cpu_decoder_4x16_1_out_8), .V(cpu_decoder_4x16_2_out_4), .S(S), .E(E), .I(I), .RESET(RESET), .O(O));  // open: OP
  CPU_REG_BYTE cpu_reg_byte_216 (
    .H(cpu_decoder_4x16_1_out_9), .V(cpu_decoder_4x16_2_out_4), .S(S), .E(E), .I(I), .RESET(RESET), .O(O));  // open: OP
  CPU_REG_BYTE cpu_reg_byte_217 (
    .H(cpu_decoder_4x16_1_out_10), .V(cpu_decoder_4x16_2_out_4), .S(S), .E(E), .I(I), .RESET(RESET), .O(O));  // open: OP
  CPU_REG_BYTE cpu_reg_byte_218 (
    .H(cpu_decoder_4x16_1_out_11), .V(cpu_decoder_4x16_2_out_4), .S(S), .E(E), .I(I), .RESET(RESET), .O(O));  // open: OP
  CPU_REG_BYTE cpu_reg_byte_219 (
    .H(cpu_decoder_4x16_1_out_12), .V(cpu_decoder_4x16_2_out_4), .S(S), .E(E), .I(I), .RESET(RESET), .O(O));  // open: OP
  CPU_REG_BYTE cpu_reg_byte_220 (
    .H(cpu_decoder_4x16_1_out_13), .V(cpu_decoder_4x16_2_out_4), .S(S), .E(E), .I(I), .RESET(RESET), .O(O));  // open: OP
  CPU_REG_BYTE cpu_reg_byte_221 (
    .H(cpu_decoder_4x16_1_out_14), .V(cpu_decoder_4x16_2_out_4), .S(S), .E(E), .I(I), .RESET(RESET), .O(O));  // open: OP
  CPU_REG_BYTE cpu_reg_byte_222 (
    .H(cpu_decoder_4x16_1_out_15), .V(cpu_decoder_4x16_2_out_4), .S(S), .E(E), .I(I), .RESET(RESET), .O(O));  // open: OP
  CPU_REG_BYTE cpu_reg_byte_223 (
    .H(cpu_decoder_4x16_1_out_16), .V(cpu_decoder_4x16_2_out_4), .S(S), .E(E), .I(I), .RESET(RESET), .O(O));  // open: OP
  CPU_REG_BYTE cpu_reg_byte_224 (
    .H(cpu_decoder_4x16_1_out_17), .V(cpu_decoder_4x16_2_out_4), .S(S), .E(E), .I(I), .RESET(RESET), .O(O));  // open: OP
  CPU_REG_BYTE cpu_reg_byte_225 (
    .H(cpu_decoder_4x16_1_out_2), .V(cpu_decoder_4x16_2_out_3), .S(S), .E(E), .I(I), .RESET(RESET), .O(O));  // open: OP
  CPU_REG_BYTE cpu_reg_byte_226 (
    .H(cpu_decoder_4x16_1_out_3), .V(cpu_decoder_4x16_2_out_3), .S(S), .E(E), .I(I), .RESET(RESET), .O(O));  // open: OP
  CPU_REG_BYTE cpu_reg_byte_227 (
    .H(cpu_decoder_4x16_1_out_4), .V(cpu_decoder_4x16_2_out_3), .S(S), .E(E), .I(I), .RESET(RESET), .O(O));  // open: OP
  CPU_REG_BYTE cpu_reg_byte_228 (
    .H(cpu_decoder_4x16_1_out_5), .V(cpu_decoder_4x16_2_out_3), .S(S), .E(E), .I(I), .RESET(RESET), .O(O));  // open: OP
  CPU_REG_BYTE cpu_reg_byte_229 (
    .H(cpu_decoder_4x16_1_out_6), .V(cpu_decoder_4x16_2_out_3), .S(S), .E(E), .I(I), .RESET(RESET), .O(O));  // open: OP
  CPU_REG_BYTE cpu_reg_byte_230 (
    .H(cpu_decoder_4x16_1_out_7), .V(cpu_decoder_4x16_2_out_3), .S(S), .E(E), .I(I), .RESET(RESET), .O(O));  // open: OP
  CPU_REG_BYTE cpu_reg_byte_231 (
    .H(cpu_decoder_4x16_1_out_8), .V(cpu_decoder_4x16_2_out_3), .S(S), .E(E), .I(I), .RESET(RESET), .O(O));  // open: OP
  CPU_REG_BYTE cpu_reg_byte_232 (
    .H(cpu_decoder_4x16_1_out_9), .V(cpu_decoder_4x16_2_out_3), .S(S), .E(E), .I(I), .RESET(RESET), .O(O));  // open: OP
  CPU_REG_BYTE cpu_reg_byte_233 (
    .H(cpu_decoder_4x16_1_out_10), .V(cpu_decoder_4x16_2_out_3), .S(S), .E(E), .I(I), .RESET(RESET), .O(O));  // open: OP
  CPU_REG_BYTE cpu_reg_byte_234 (
    .H(cpu_decoder_4x16_1_out_11), .V(cpu_decoder_4x16_2_out_3), .S(S), .E(E), .I(I), .RESET(RESET), .O(O));  // open: OP
  CPU_REG_BYTE cpu_reg_byte_235 (
    .H(cpu_decoder_4x16_1_out_12), .V(cpu_decoder_4x16_2_out_3), .S(S), .E(E), .I(I), .RESET(RESET), .O(O));  // open: OP
  CPU_REG_BYTE cpu_reg_byte_236 (
    .H(cpu_decoder_4x16_1_out_13), .V(cpu_decoder_4x16_2_out_3), .S(S), .E(E), .I(I), .RESET(RESET), .O(O));  // open: OP
  CPU_REG_BYTE cpu_reg_byte_237 (
    .H(cpu_decoder_4x16_1_out_14), .V(cpu_decoder_4x16_2_out_3), .S(S), .E(E), .I(I), .RESET(RESET), .O(O));  // open: OP
  CPU_REG_BYTE cpu_reg_byte_238 (
    .H(cpu_decoder_4x16_1_out_15), .V(cpu_decoder_4x16_2_out_3), .S(S), .E(E), .I(I), .RESET(RESET), .O(O));  // open: OP
  CPU_REG_BYTE cpu_reg_byte_239 (
    .H(cpu_decoder_4x16_1_out_16), .V(cpu_decoder_4x16_2_out_3), .S(S), .E(E), .I(I), .RESET(RESET), .O(O));  // open: OP
  CPU_REG_BYTE cpu_reg_byte_240 (
    .H(cpu_decoder_4x16_1_out_17), .V(cpu_decoder_4x16_2_out_3), .S(S), .E(E), .I(I), .RESET(RESET), .O(O));  // open: OP
  CPU_REG_BYTE cpu_reg_byte_241 (
    .H(cpu_decoder_4x16_1_out_2), .V(cpu_decoder_4x16_2_out_2), .S(S), .E(E), .I(I), .RESET(RESET), .O(O));  // open: OP
  CPU_REG_BYTE cpu_reg_byte_242 (
    .H(cpu_decoder_4x16_1_out_3), .V(cpu_decoder_4x16_2_out_2), .S(S), .E(E), .I(I), .RESET(RESET), .O(O));  // open: OP
  CPU_REG_BYTE cpu_reg_byte_243 (
    .H(cpu_decoder_4x16_1_out_4), .V(cpu_decoder_4x16_2_out_2), .S(S), .E(E), .I(I), .RESET(RESET), .O(O));  // open: OP
  CPU_REG_BYTE cpu_reg_byte_244 (
    .H(cpu_decoder_4x16_1_out_5), .V(cpu_decoder_4x16_2_out_2), .S(S), .E(E), .I(I), .RESET(RESET), .O(O));  // open: OP
  CPU_REG_BYTE cpu_reg_byte_245 (
    .H(cpu_decoder_4x16_1_out_6), .V(cpu_decoder_4x16_2_out_2), .S(S), .E(E), .I(I), .RESET(RESET), .O(O));  // open: OP
  CPU_REG_BYTE cpu_reg_byte_246 (
    .H(cpu_decoder_4x16_1_out_7), .V(cpu_decoder_4x16_2_out_2), .S(S), .E(E), .I(I), .RESET(RESET), .O(O));  // open: OP
  CPU_REG_BYTE cpu_reg_byte_247 (
    .H(cpu_decoder_4x16_1_out_8), .V(cpu_decoder_4x16_2_out_2), .S(S), .E(E), .I(I), .RESET(RESET), .O(O));  // open: OP
  CPU_REG_BYTE cpu_reg_byte_248 (
    .H(cpu_decoder_4x16_1_out_9), .V(cpu_decoder_4x16_2_out_2), .S(S), .E(E), .I(I), .RESET(RESET), .O(O));  // open: OP
  CPU_REG_BYTE cpu_reg_byte_249 (
    .H(cpu_decoder_4x16_1_out_10), .V(cpu_decoder_4x16_2_out_2), .S(S), .E(E), .I(I), .RESET(RESET), .O(O));  // open: OP
  CPU_REG_BYTE cpu_reg_byte_250 (
    .H(cpu_decoder_4x16_1_out_11), .V(cpu_decoder_4x16_2_out_2), .S(S), .E(E), .I(I), .RESET(RESET), .O(O));  // open: OP
  CPU_REG_BYTE cpu_reg_byte_251 (
    .H(cpu_decoder_4x16_1_out_12), .V(cpu_decoder_4x16_2_out_2), .S(S), .E(E), .I(I), .RESET(RESET), .O(O));  // open: OP
  CPU_REG_BYTE cpu_reg_byte_252 (
    .H(cpu_decoder_4x16_1_out_13), .V(cpu_decoder_4x16_2_out_2), .S(S), .E(E), .I(I), .RESET(RESET), .O(O));  // open: OP
  CPU_REG_BYTE cpu_reg_byte_253 (
    .H(cpu_decoder_4x16_1_out_14), .V(cpu_decoder_4x16_2_out_2), .S(S), .E(E), .I(I), .RESET(RESET), .O(O));  // open: OP
  CPU_REG_BYTE cpu_reg_byte_254 (
    .H(cpu_decoder_4x16_1_out_15), .V(cpu_decoder_4x16_2_out_2), .S(S), .E(E), .I(I), .RESET(RESET), .O(O));  // open: OP
  CPU_REG_BYTE cpu_reg_byte_255 (
    .H(cpu_decoder_4x16_1_out_16), .V(cpu_decoder_4x16_2_out_2), .S(S), .E(E), .I(I), .RESET(RESET), .O(O));  // open: OP
  CPU_REG_BYTE cpu_reg_byte_256 (
    .H(cpu_decoder_4x16_1_out_17), .V(cpu_decoder_4x16_2_out_2), .S(S), .E(E), .I(I), .RESET(RESET), .O(O));  // open: OP

  // Notes on the sheet:
  //   256 BYTE RAM. Not used in the actual CPU since Logisim freaks out at the size of the bloody thing. Built it just to see how it works.
endmodule

module CPU_DECODER_2x4 (
  input  [1:0] AB,
  output out_2,
  output out_3,
  output out_4,
  output out_5
);

  wire not_1_out, not_2_out;

  not not_1 (not_1_out, AB[1]);
  not not_2 (not_2_out, AB[0]);
  and FF (out_2, not_1_out, not_2_out);
  and FT (out_3, not_1_out, AB[0]);
  and TF (out_4, AB[1], not_2_out);
  and TT (out_5, AB[1], AB[0]);

  // Notes on the sheet:
  //   A
  //   !A
  //   B
  //   !B
endmodule

module CPU_DECODER_3x8 (
  input  [2:0] I,
  output out_2,
  output out_3,
  output out_4,
  output out_5,
  output out_6,
  output out_7,
  output out_8,
  output out_9
);

  wire not_1_out, not_2_out, not_3_out;

  not not_1 (not_1_out, I[2]);
  not not_2 (not_2_out, I[1]);
  not not_3 (not_3_out, I[0]);
  and FFF (out_2, not_1_out, not_2_out, not_3_out);
  and FFT (out_3, not_1_out, not_2_out, I[0]);
  and FTF (out_4, not_1_out, I[1], not_3_out);
  and FTT (out_5, not_1_out, I[1], I[0]);
  and TFF (out_6, I[2], not_2_out, not_3_out);
  and TFT (out_7, I[2], not_2_out, I[0]);
  and TTF (out_8, I[2], I[1], not_3_out);
  and TTT (out_9, I[2], I[1], I[0]);

  // Notes on the sheet:
  //   A
  //   B
  //   C
  //   !A
  //   !B
  //   !C
endmodule

module CPU_DECODER_4x16 (
  input  [3:0] I,
  output out_2,
  output out_3,
  output out_4,
  output out_5,
  output out_6,
  output out_7,
  output out_8,
  output out_9,
  output out_10,
  output out_11,
  output out_12,
  output out_13,
  output out_14,
  output out_15,
  output out_16,
  output out_17
);

  wire not_1_out, not_2_out, not_3_out, not_4_out;

  not not_1 (not_1_out, I[3]);
  not not_2 (not_2_out, I[2]);
  not not_3 (not_3_out, I[1]);
  not not_4 (not_4_out, I[0]);
  and FFFF (out_2, not_1_out, not_2_out, not_3_out, not_4_out);
  and FFFT (out_3, not_1_out, not_2_out, not_3_out, I[0]);
  and FFTF (out_4, not_1_out, not_2_out, I[1], not_4_out);
  and FFTT (out_5, not_1_out, not_2_out, I[1], I[0]);
  and FTFF (out_6, not_1_out, I[2], not_3_out, not_4_out);
  and FTFT (out_7, not_1_out, I[2], not_3_out, I[0]);
  and FTTF (out_8, not_1_out, I[2], I[1], not_4_out);
  and FTTT (out_9, not_1_out, I[2], I[1], I[0]);
  and TFFF (out_10, I[3], not_2_out, not_3_out, not_4_out);
  and TFFT (out_11, I[3], not_2_out, not_3_out, I[0]);
  and TFTF (out_12, I[3], not_2_out, I[1], not_4_out);
  and TFTT (out_13, I[3], not_2_out, I[1], I[0]);
  and TTFF (out_14, I[3], I[2], not_3_out, not_4_out);
  and TTFT (out_15, I[3], I[2], not_3_out, I[0]);
  and TTTF (out_16, I[3], I[2], I[1], not_4_out);
  and TTTT (out_17, I[3], I[2], I[1], I[0]);

  // Notes on the sheet:
  //   A
  //   B
  //   C
  //   D
  //   !A
  //   !B
  //   !C
  //   !D
endmodule

module CPU_ADDER (
  input  A,
  input  B,
  input  CarryIn,
  output Sum,
  output CarryOut
);

  wire and_1_out, and_2_out, xor_1_out;

  xor xor_1 (xor_1_out, A, B);
  and and_1 (and_1_out, CarryIn, xor_1_out);
  and and_2 (and_2_out, A, B);
  xor xor_2 (Sum, xor_1_out, CarryIn);
  or or_1 (CarryOut, and_1_out, and_2_out);
endmodule

module CPU_ADDER_8 (
  input  [7:0] A,
  input  [7:0] B,
  input  CarryIn,
  output CarryOut,
  output [7:0] SUM
);

  wire cpu_adder_2_carryout, cpu_adder_3_carryout, cpu_adder_4_carryout, cpu_adder_5_carryout,
       cpu_adder_6_carryout, cpu_adder_7_carryout, cpu_adder_8_carryout;

  CPU_ADDER cpu_adder_1 (.A(A[7]), .B(B[7]), .CarryIn(cpu_adder_2_carryout), .Sum(SUM[7]), .CarryOut(CarryOut));
  CPU_ADDER cpu_adder_2 (
    .A(A[6]), .B(B[6]), .CarryIn(cpu_adder_3_carryout), .Sum(SUM[6]), .CarryOut(cpu_adder_2_carryout));
  CPU_ADDER cpu_adder_3 (
    .A(A[5]), .B(B[5]), .CarryIn(cpu_adder_4_carryout), .Sum(SUM[5]), .CarryOut(cpu_adder_3_carryout));
  CPU_ADDER cpu_adder_4 (
    .A(A[4]), .B(B[4]), .CarryIn(cpu_adder_5_carryout), .Sum(SUM[4]), .CarryOut(cpu_adder_4_carryout));
  CPU_ADDER cpu_adder_5 (
    .A(A[3]), .B(B[3]), .CarryIn(cpu_adder_6_carryout), .Sum(SUM[3]), .CarryOut(cpu_adder_5_carryout));
  CPU_ADDER cpu_adder_6 (
    .A(A[2]), .B(B[2]), .CarryIn(cpu_adder_7_carryout), .Sum(SUM[2]), .CarryOut(cpu_adder_6_carryout));
  CPU_ADDER cpu_adder_7 (
    .A(A[1]), .B(B[1]), .CarryIn(cpu_adder_8_carryout), .Sum(SUM[1]), .CarryOut(cpu_adder_7_carryout));
  CPU_ADDER cpu_adder_8 (.A(A[0]), .B(B[0]), .CarryIn(CarryIn), .Sum(SUM[0]), .CarryOut(cpu_adder_8_carryout));
endmodule

module CPU_SHL (
  input  ShiftIn,
  input  [7:0] I,
  output [7:0] O,
  output ShiftOut
);

  wire [6:0] cpu_register_8_custom_1_o;

  CPU_REGISTER_8_CUSTOM cpu_register_8_custom_1 (
    .I(I), .S(1'b1), .E(1'b1), .O({ShiftOut, cpu_register_8_custom_1_o}));  // open: out_4, REG_VAL
  CPU_REGISTER_8_CUSTOM cpu_register_8_custom_2 (
    .I({cpu_register_8_custom_1_o, ShiftIn}), .S(1'b1), .E(1'b1), .O(O));  // open: out_4, REG_VAL
endmodule

module CPU_SHR (
  input  [7:0] I,
  input  ShiftIn,
  output ShiftOut,
  output [7:0] O
);

  wire [7:1] cpu_register_8_custom_1_o;

  CPU_REGISTER_8_CUSTOM cpu_register_8_custom_1 (
    .I(I), .S(1'b1), .E(1'b1), .O({cpu_register_8_custom_1_o, ShiftOut}));  // open: out_4, REG_VAL
  CPU_REGISTER_8_CUSTOM cpu_register_8_custom_2 (
    .I({ShiftIn, cpu_register_8_custom_1_o}), .S(1'b1), .E(1'b1), .O(O));  // open: out_4, REG_VAL
endmodule

module CPU_NOT (
  input  [7:0] I,
  output [7:0] O
);

  not not_1 (O[0], I[0]);
  not not_2 (O[1], I[1]);
  not not_3 (O[2], I[2]);
  not not_4 (O[3], I[3]);
  not not_5 (O[4], I[4]);
  not not_6 (O[5], I[5]);
  not not_7 (O[6], I[6]);
  not not_8 (O[7], I[7]);
endmodule

module CPU_AND (
  input  [7:0] A,
  input  [7:0] B,
  output [7:0] O
);

  and and_1 (O[0], A[0], B[0]);
  and and_2 (O[1], A[1], B[1]);
  and and_3 (O[2], A[2], B[2]);
  and and_4 (O[3], A[3], B[3]);
  and and_5 (O[4], A[4], B[4]);
  and and_6 (O[5], A[5], B[5]);
  and and_7 (O[6], A[6], B[6]);
  and and_8 (O[7], A[7], B[7]);
endmodule

module CPU_OR (
  input  [7:0] A,
  input  [7:0] B,
  output [7:0] O
);

  or or_1 (O[0], A[0], B[0]);
  or or_2 (O[1], A[1], B[1]);
  or or_3 (O[2], A[2], B[2]);
  or or_4 (O[3], A[3], B[3]);
  or or_5 (O[4], A[4], B[4]);
  or or_6 (O[5], A[5], B[5]);
  or or_7 (O[6], A[6], B[6]);
  or or_8 (O[7], A[7], B[7]);
endmodule

module CPU_XOR_LE_1 (
  input  AboveEqual,
  input  A_Larger,
  input  A,
  input  B,
  output C,
  output Equal,
  output A_Large
);

  wire and_2_out, not_1_out;

  xor xor_1 (C, A, B);
  not not_1 (not_1_out, C);
  and and_1 (Equal, not_1_out, AboveEqual);
  and and_2 (and_2_out, AboveEqual, A, C);
  xor xor_2 (A_Large, and_2_out, A_Larger);
endmodule

module CPU_XOR_LE_8 (
  input  [7:0] A,
  input  [7:0] B,
  output [7:0] O,
  output Larger,
  output Equal
);

  wire cpu_xor_le_1_1_a_large, cpu_xor_le_1_1_equal, cpu_xor_le_1_2_a_large, cpu_xor_le_1_2_equal,
       cpu_xor_le_1_3_a_large, cpu_xor_le_1_3_equal, cpu_xor_le_1_4_a_large, cpu_xor_le_1_4_equal,
       cpu_xor_le_1_5_a_large, cpu_xor_le_1_5_equal, cpu_xor_le_1_6_a_large, cpu_xor_le_1_6_equal,
       cpu_xor_le_1_7_a_large, cpu_xor_le_1_7_equal;

  CPU_XOR_LE_1 cpu_xor_le_1_1 (
    .A(A[0]), .B(B[0]), .AboveEqual(1'b1), .A_Larger(1'b0), .Equal(cpu_xor_le_1_1_equal),
    .A_Large(cpu_xor_le_1_1_a_large), .C(O[0]));
  CPU_XOR_LE_1 cpu_xor_le_1_2 (
    .A(A[1]), .B(B[1]), .AboveEqual(cpu_xor_le_1_1_equal), .A_Larger(cpu_xor_le_1_1_a_large),
    .Equal(cpu_xor_le_1_2_equal), .A_Large(cpu_xor_le_1_2_a_large), .C(O[1]));
  CPU_XOR_LE_1 cpu_xor_le_1_3 (
    .A(A[2]), .B(B[2]), .AboveEqual(cpu_xor_le_1_2_equal), .A_Larger(cpu_xor_le_1_2_a_large),
    .Equal(cpu_xor_le_1_3_equal), .A_Large(cpu_xor_le_1_3_a_large), .C(O[2]));
  CPU_XOR_LE_1 cpu_xor_le_1_4 (
    .A(A[3]), .B(B[3]), .AboveEqual(cpu_xor_le_1_3_equal), .A_Larger(cpu_xor_le_1_3_a_large),
    .Equal(cpu_xor_le_1_4_equal), .A_Large(cpu_xor_le_1_4_a_large), .C(O[3]));
  CPU_XOR_LE_1 cpu_xor_le_1_5 (
    .A(A[4]), .B(B[4]), .AboveEqual(cpu_xor_le_1_4_equal), .A_Larger(cpu_xor_le_1_4_a_large),
    .Equal(cpu_xor_le_1_5_equal), .A_Large(cpu_xor_le_1_5_a_large), .C(O[4]));
  CPU_XOR_LE_1 cpu_xor_le_1_6 (
    .A(A[5]), .B(B[5]), .AboveEqual(cpu_xor_le_1_5_equal), .A_Larger(cpu_xor_le_1_5_a_large),
    .Equal(cpu_xor_le_1_6_equal), .A_Large(cpu_xor_le_1_6_a_large), .C(O[5]));
  CPU_XOR_LE_1 cpu_xor_le_1_7 (
    .A(A[6]), .B(B[6]), .AboveEqual(cpu_xor_le_1_6_equal), .A_Larger(cpu_xor_le_1_6_a_large),
    .Equal(cpu_xor_le_1_7_equal), .A_Large(cpu_xor_le_1_7_a_large), .C(O[6]));
  CPU_XOR_LE_1 cpu_xor_le_1_8 (
    .A(A[7]), .B(B[7]), .AboveEqual(cpu_xor_le_1_7_equal), .A_Larger(cpu_xor_le_1_7_a_large), .Equal(Equal),
    .A_Large(Larger), .C(O[7]));
endmodule

module CPU_Z (
  input  [7:0] I,
  output O
);

  wire or_1_out;

  or or_1 (or_1_out, I[0], I[1], I[2], I[3], I[4], I[5], I[6], I[7]);
  not not_1 (O, or_1_out);
endmodule

module CPU_ALU (
  input  [7:0] A,
  input  [7:0] B,
  input  CarryIn,
  input  B2,
  input  B1,
  input  B0,
  output A_Larger,
  output EQUAL,
  output ZERO,
  output [7:0] O,
  output CarryOut
);

  wire and_1_out, and_2_out, and_3_out, cpu_adder_8_1_carryout, cpu_decoder_3x8_1_out_2,
       cpu_decoder_3x8_1_out_3, cpu_decoder_3x8_1_out_4, cpu_decoder_3x8_1_out_5, cpu_decoder_3x8_1_out_6,
       cpu_decoder_3x8_1_out_7, cpu_decoder_3x8_1_out_8, cpu_shl_1_shiftout, cpu_shr_1_shiftout;
  wire [7:0] cpu_adder_8_1_sum, cpu_and_1_o, cpu_not_1_o, cpu_or_1_o, cpu_shl_1_o, cpu_shr_1_o,
       cpu_xor_le_8_1_o;

  CPU_XOR_LE_8 cpu_xor_le_8_1 (.A(A), .B(B), .Larger(A_Larger), .Equal(EQUAL), .O(cpu_xor_le_8_1_o));
  CPU_OR cpu_or_1 (.B(B), .A(A), .O(cpu_or_1_o));
  CPU_AND cpu_and_1 (.B(B), .A(A), .O(cpu_and_1_o));
  CPU_NOT cpu_not_1 (.I(A), .O(cpu_not_1_o));
  CPU_SHL cpu_shl_1 (.I(A), .ShiftIn(CarryIn), .ShiftOut(cpu_shl_1_shiftout), .O(cpu_shl_1_o));
  CPU_SHR cpu_shr_1 (.I(A), .ShiftIn(CarryIn), .ShiftOut(cpu_shr_1_shiftout), .O(cpu_shr_1_o));
  CPU_ADDER_8 cpu_adder_8_1 (
    .A(A), .B(B), .CarryIn(CarryIn), .CarryOut(cpu_adder_8_1_carryout), .SUM(cpu_adder_8_1_sum));
  CPU_DECODER_3x8 cpu_decoder_3x8_1 (
    .I({B2, B1, B0}), .out_2(cpu_decoder_3x8_1_out_2), .out_3(cpu_decoder_3x8_1_out_3),
    .out_4(cpu_decoder_3x8_1_out_4), .out_5(cpu_decoder_3x8_1_out_5), .out_6(cpu_decoder_3x8_1_out_6),
    .out_7(cpu_decoder_3x8_1_out_7), .out_8(cpu_decoder_3x8_1_out_8));  // open: out_9
  CPU_ENABLER cpu_enabler_1 (.I(cpu_xor_le_8_1_o), .E(cpu_decoder_3x8_1_out_8), .O(O));
  CPU_ENABLER cpu_enabler_2 (.I(cpu_or_1_o), .E(cpu_decoder_3x8_1_out_7), .O(O));
  CPU_ENABLER cpu_enabler_3 (.I(cpu_and_1_o), .E(cpu_decoder_3x8_1_out_6), .O(O));
  CPU_ENABLER cpu_enabler_4 (.I(cpu_not_1_o), .E(cpu_decoder_3x8_1_out_5), .O(O));
  CPU_ENABLER cpu_enabler_5 (.I(cpu_shl_1_o), .E(cpu_decoder_3x8_1_out_4), .O(O));
  CPU_ENABLER cpu_enabler_6 (.I(cpu_shr_1_o), .E(cpu_decoder_3x8_1_out_3), .O(O));
  CPU_ENABLER cpu_enabler_7 (.I(cpu_adder_8_1_sum), .E(cpu_decoder_3x8_1_out_2), .O(O));
  and and_1 (and_1_out, cpu_shl_1_shiftout, cpu_decoder_3x8_1_out_4);
  and and_2 (and_2_out, cpu_shr_1_shiftout, cpu_decoder_3x8_1_out_3);
  and and_3 (and_3_out, cpu_adder_8_1_carryout, cpu_decoder_3x8_1_out_2);
  assign CarryOut = cpu_decoder_3x8_1_out_4 ? and_1_out : 1'bz;  // Controlled_Buffer controlled_buffer_1
  assign CarryOut = cpu_decoder_3x8_1_out_3 ? and_2_out : 1'bz;  // Controlled_Buffer controlled_buffer_2
  assign CarryOut = cpu_decoder_3x8_1_out_2 ? and_3_out : 1'bz;  // Controlled_Buffer controlled_buffer_3
  CPU_Z cpu_z_1 (.I(O), .O(ZERO));
endmodule

module CPU_ALU_FLAGS (
  input  C,
  input  AL,
  input  EQ,
  input  Z,
  input  S,
  output C_OUT,
  output AL_OUT,
  output EQ_OUT,
  output Z_OUT
);

  Register #(.trigger("high"), .width(1)) register_1 (.D(C), .clk(S), .Q(C_OUT));  // open: en, clr
  Register #(.trigger("high"), .width(1)) register_2 (.D(AL), .clk(S), .Q(AL_OUT));  // open: en, clr
  Register #(.trigger("high"), .width(1)) register_3 (.D(EQ), .clk(S), .Q(EQ_OUT));  // open: en, clr
  Register #(.trigger("high"), .width(1)) register_4 (.D(Z), .clk(S), .Q(Z_OUT));  // open: en, clr
endmodule

module CPU_CLK (
  input  CLKIN,
  output CLK,
  output CLKS,
  output CLKE
);

  wire j_k_ff_1_qn, nand_1_out;

  J_K_Flip_Flop j_k_ff_1 (.J(1'b1), .K(1'b1), .clk(CLKIN), .Q(CLK), .Qn(j_k_ff_1_qn));  // open: preset, reset
  nand nand_1 (nand_1_out, CLKIN, CLK);
  nand nand_2 (CLKE, j_k_ff_1_qn, CLKIN);
  not not_1 (CLKS, nand_1_out);
endmodule

module CPU_CARRY_TMP (
  input  C,
  input  S,
  output O
);

  Register #(.trigger("high"), .width(1)) register_1 (.D(C), .clk(S), .Q(O));  // open: en, clr
endmodule
